// Logisim project mlp10.circ as structural Verilog: 5 circuits, main circuit main
module main (
  input  [31:0] A
);

  wire and_1_out, and_2_out, and_3_out, button_1_out, clk_out, counter_1_carry, counter_2_carry,
       counter_3_carry, counter_4_carry, counter_5_carry, d_ff_1_q, d_ff_1_qn, multiplexer_1_out,
       multiplexer_2_out;
  wire [3:0] bit_extender_1_out, counter_5_q, max10_1_out_11, multiplexer_4_out;
  wire [4:0] counter_1_q, counter_3_q;
  wire [9:0] counter_2_q;
  wire [15:0] rom_2_data, rom_3_data, rom_4_data, rom_5_data, rom_6_data, rom_7_data, rom_8_data, rom_9_data,
       rom_10_data, rom_11_data, rom_12_data, rom_13_data, rom_14_data, rom_15_data, rom_16_data,
       rom_17_data, rom_18_data, rom_19_data, rom_20_data, rom_21_data;
  wire [27:0] rf_1_out_6, rf_1_out_7, rf_1_out_8, rf_1_out_9, rf_1_out_10, rf_1_out_11, rf_1_out_12,
       rf_1_out_13, rf_1_out_14, rf_1_out_15, rf_1_out_16, rf_1_out_17, rf_1_out_18, rf_1_out_19,
       rf_1_out_20, rf_1_out_21, rf_1_out_22, rf_1_out_23, rf_1_out_24, rf_1_out_25, rf_1_out_26,
       rf_1_out_27, rf_1_out_28, rf_1_out_29, rf_1_out_30, rf_1_out_31, rf_1_out_32, rf_1_out_33, rom_1_data;
  wire [31:0] adder_1_out, adder_2_out, adder_3_out, adder_4_out, adder_5_out, adder_6_out, adder_7_out,
       adder_8_out, adder_9_out, adder_10_out, adder_11_out, adder_12_out, adder_13_out, adder_14_out,
       adder_15_out, adder_16_out, adder_17_out, adder_18_out, adder_19_out, adder_20_out, adder_21_out,
       adder_22_out, adder_23_out, adder_24_out, adder_25_out, adder_26_out, adder_27_out, adder_28_out,
       adder_29_out, adder_30_out, adder_31_out, adder_32_out, adder_33_out, adder_34_out, adder_35_out,
       adder_36_out, adder_37_out, adder_38_out, adder_39_out, adder_40_out, bit_extender_2_out,
       bit_extender_3_out, bit_extender_4_out, bit_extender_5_out, bit_extender_6_out, bit_extender_7_out,
       bit_extender_8_out, bit_extender_9_out, bit_extender_10_out, bit_extender_11_out, bit_extender_12_out,
       bit_extender_13_out, bit_extender_14_out, bit_extender_15_out, bit_extender_16_out,
       bit_extender_17_out, bit_extender_18_out, bit_extender_19_out, bit_extender_20_out,
       bit_extender_21_out, bit_extender_22_out, bit_extender_23_out, bit_extender_24_out,
       bit_extender_25_out, bit_extender_26_out, bit_extender_27_out, bit_extender_28_out,
       bit_extender_29_out, bit_extender_30_out, bit_extender_31_out, bit_extender_32_out,
       bit_extender_33_out, bit_extender_34_out, bit_extender_35_out, bit_extender_36_out,
       bit_extender_37_out, bit_extender_38_out, bit_extender_39_out, bit_extender_40_out,
       bit_extender_41_out, bit_extender_42_out, multiplexer_3_out, multiplexer_5_out, multiplier_1_out,
       multiplier_2_out, multiplier_3_out, multiplier_4_out, multiplier_5_out, multiplier_6_out,
       multiplier_7_out, multiplier_8_out, multiplier_9_out, multiplier_10_out, multiplier_11_out,
       multiplier_12_out, multiplier_13_out, multiplier_14_out, multiplier_15_out, multiplier_16_out,
       multiplier_17_out, multiplier_18_out, multiplier_19_out, multiplier_20_out, register_1_q,
       register_2_q, register_3_q, register_4_q, register_5_q, register_6_q, register_7_q, register_8_q,
       register_9_q, register_10_q, register_11_q, register_12_q, register_13_q, register_14_q,
       register_15_q, register_16_q, register_17_q, register_18_q, register_19_q, register_20_q,
       relu_1_out_2, relu_2_out_2, relu_3_out_2, relu_4_out_2, relu_5_out_2, relu_6_out_2, relu_7_out_2,
       relu_8_out_2, relu_9_out_2, relu_10_out_2, relu_11_out_2, relu_12_out_2, relu_13_out_2, relu_14_out_2,
       relu_15_out_2, relu_16_out_2, relu_17_out_2, relu_18_out_2, relu_19_out_2, relu_20_out_2;

  Clock clk (.out(clk_out));
  Button button_1 (.out(button_1_out));
  Counter #(.width(5), .max('h1b)) counter_1 (
    .count(counter_3_carry), .Q(counter_1_q), .carry(counter_1_carry), .clk(multiplexer_1_out),
    .clr(button_1_out));  // open: load, D
  Multiplexer #(.enable("false")) multiplexer_1 (
    .in0(clk_out), .in1(1'b0), .out(multiplexer_1_out), .sel(counter_4_carry));
  and and_1 (and_1_out, counter_1_carry, counter_2_carry);
  Counter #(.width(10), .max('h30f)) counter_2 (
    .Q(counter_2_q), .carry(counter_2_carry), .clk(multiplexer_1_out), .clr(button_1_out));  // open: load, D, count
  D_Flip_Flop d_ff_1 (
    .clk(and_1_out), .D(1'b1), .Q(d_ff_1_q), .Qn(d_ff_1_qn), .reset(button_1_out));  // open: preset, en
  Counter #(.width(5), .max('h1b)) counter_3 (
    .Q(counter_3_q), .carry(counter_3_carry), .clk(multiplexer_1_out), .clr(button_1_out));  // open: load, D, count
  Hex_Digit_Display hex_digit_display_1 (.value(bit_extender_1_out));  // open: dp
  assign bit_extender_1_out = {{3{1'b0}}, counter_1_q[4]};  // Bit_Extender bit_extender_1
  ROM #(.addrWidth(5), .dataWidth(28)) rom_1 (.addr(counter_1_q), .data(rom_1_data));  // open: sel
  Hex_Digit_Display hex_digit_display_2 (.value(counter_1_q[3:0]));  // open: dp
  ROM #(.addrWidth(10), .dataWidth(16)) rom_2 (.addr(counter_2_q), .data(rom_2_data));  // open: sel
  ROM #(.addrWidth(10), .dataWidth(16)) rom_3 (.addr(counter_2_q), .data(rom_3_data));  // open: sel
  ROM #(.addrWidth(10), .dataWidth(16)) rom_4 (.addr(counter_2_q), .data(rom_4_data));  // open: sel
  ROM #(.addrWidth(10), .dataWidth(16)) rom_5 (.addr(counter_2_q), .data(rom_5_data));  // open: sel
  ROM #(.addrWidth(10), .dataWidth(16)) rom_6 (.addr(counter_2_q), .data(rom_6_data));  // open: sel
  ROM #(.addrWidth(10), .dataWidth(16)) rom_7 (.addr(counter_2_q), .data(rom_7_data));  // open: sel
  ROM #(.addrWidth(10), .dataWidth(16)) rom_8 (.addr(counter_2_q), .data(rom_8_data));  // open: sel
  ROM #(.addrWidth(10), .dataWidth(16)) rom_9 (.addr(counter_2_q), .data(rom_9_data));  // open: sel
  ROM #(.addrWidth(10), .dataWidth(16)) rom_10 (.addr(counter_2_q), .data(rom_10_data));  // open: sel
  ROM #(.addrWidth(10), .dataWidth(16)) rom_11 (.addr(counter_2_q), .data(rom_11_data));  // open: sel
  Multiplexer #(.select(5), .enable("false")) multiplexer_2 (
    .in0(rom_1_data[27]), .in1(rom_1_data[26]), .in2(rom_1_data[25]), .in3(rom_1_data[24]),
    .in4(rom_1_data[23]), .in5(rom_1_data[22]), .in6(rom_1_data[21]), .in7(rom_1_data[20]),
    .in8(rom_1_data[19]), .in9(rom_1_data[18]), .in10(rom_1_data[17]), .in11(rom_1_data[16]),
    .in12(rom_1_data[15]), .in13(rom_1_data[14]), .in14(rom_1_data[13]), .in15(rom_1_data[12]),
    .in16(rom_1_data[11]), .in17(rom_1_data[10]), .in18(rom_1_data[9]), .in19(rom_1_data[8]),
    .in20(rom_1_data[7]), .in21(rom_1_data[6]), .in22(rom_1_data[5]), .in23(rom_1_data[4]),
    .in24(rom_1_data[3]), .in25(rom_1_data[2]), .in26(rom_1_data[1]), .in27(rom_1_data[0]),
    .out(multiplexer_2_out), .sel(counter_3_q));  // open: in28, in29, in30, in31
  assign bit_extender_2_out = {{16{rom_2_data[15]}}, rom_2_data};  // Bit_Extender bit_extender_2
  assign bit_extender_3_out = {{16{rom_3_data[15]}}, rom_3_data};  // Bit_Extender bit_extender_3
  assign bit_extender_4_out = {{16{rom_4_data[15]}}, rom_4_data};  // Bit_Extender bit_extender_4
  assign bit_extender_5_out = {{16{rom_5_data[15]}}, rom_5_data};  // Bit_Extender bit_extender_5
  assign bit_extender_6_out = {{16{rom_6_data[15]}}, rom_6_data};  // Bit_Extender bit_extender_6
  assign bit_extender_7_out = {{16{rom_7_data[15]}}, rom_7_data};  // Bit_Extender bit_extender_7
  assign bit_extender_8_out = {{16{rom_8_data[15]}}, rom_8_data};  // Bit_Extender bit_extender_8
  assign bit_extender_9_out = {{16{rom_9_data[15]}}, rom_9_data};  // Bit_Extender bit_extender_9
  assign bit_extender_10_out = {{16{rom_10_data[15]}}, rom_10_data};  // Bit_Extender bit_extender_10
  assign bit_extender_11_out = {{16{rom_11_data[15]}}, rom_11_data};  // Bit_Extender bit_extender_11
  assign bit_extender_12_out = {{31{1'b0}}, multiplexer_2_out};  // Bit_Extender bit_extender_12
  Multiplier #(.width(32)) multiplier_1 (
    .a(bit_extender_12_out), .b(bit_extender_2_out), .out(multiplier_1_out));  // open: cin, cout
  Multiplier #(.width(32)) multiplier_2 (
    .a(bit_extender_12_out), .b(bit_extender_3_out), .out(multiplier_2_out));  // open: cin, cout
  Multiplier #(.width(32)) multiplier_3 (
    .a(bit_extender_12_out), .b(bit_extender_4_out), .out(multiplier_3_out));  // open: cin, cout
  Multiplier #(.width(32)) multiplier_4 (
    .a(bit_extender_12_out), .b(bit_extender_5_out), .out(multiplier_4_out));  // open: cin, cout
  Multiplier #(.width(32)) multiplier_5 (
    .a(bit_extender_12_out), .b(bit_extender_6_out), .out(multiplier_5_out));  // open: cin, cout
  Multiplier #(.width(32)) multiplier_6 (
    .a(bit_extender_12_out), .b(bit_extender_7_out), .out(multiplier_6_out));  // open: cin, cout
  Multiplier #(.width(32)) multiplier_7 (
    .a(bit_extender_12_out), .b(bit_extender_8_out), .out(multiplier_7_out));  // open: cin, cout
  Multiplier #(.width(32)) multiplier_8 (
    .a(bit_extender_12_out), .b(bit_extender_9_out), .out(multiplier_8_out));  // open: cin, cout
  Multiplier #(.width(32)) multiplier_9 (
    .a(bit_extender_12_out), .b(bit_extender_10_out), .out(multiplier_9_out));  // open: cin, cout
  Multiplier #(.width(32)) multiplier_10 (
    .a(bit_extender_12_out), .b(bit_extender_11_out), .out(multiplier_10_out));  // open: cin, cout
  and and_2 (and_2_out, d_ff_1_qn, multiplexer_1_out);
  Adder #(.width(32)) adder_1 (.a(multiplier_1_out), .b(register_1_q), .out(adder_1_out));  // open: cin, cout
  Adder #(.width(32)) adder_2 (.a(multiplier_2_out), .b(register_2_q), .out(adder_2_out));  // open: cin, cout
  Adder #(.width(32)) adder_3 (.a(multiplier_3_out), .b(register_3_q), .out(adder_3_out));  // open: cin, cout
  Adder #(.width(32)) adder_4 (.a(multiplier_4_out), .b(register_4_q), .out(adder_4_out));  // open: cin, cout
  Adder #(.width(32)) adder_5 (.a(multiplier_5_out), .b(register_5_q), .out(adder_5_out));  // open: cin, cout
  Adder #(.width(32)) adder_6 (.a(multiplier_6_out), .b(register_6_q), .out(adder_6_out));  // open: cin, cout
  Adder #(.width(32)) adder_7 (.a(multiplier_7_out), .b(register_7_q), .out(adder_7_out));  // open: cin, cout
  Adder #(.width(32)) adder_8 (.a(multiplier_8_out), .b(register_8_q), .out(adder_8_out));  // open: cin, cout
  Adder #(.width(32)) adder_9 (.a(multiplier_9_out), .b(register_9_q), .out(adder_9_out));  // open: cin, cout
  Adder #(.width(32)) adder_10 (.a(multiplier_10_out), .b(register_10_q), .out(adder_10_out));  // open: cin, cout
  Register #(.width(32)) register_1 (
    .D(adder_1_out), .Q(register_1_q), .clk(and_2_out), .clr(button_1_out));  // open: en
  Register #(.width(32)) register_2 (
    .D(adder_2_out), .Q(register_2_q), .clk(and_2_out), .clr(button_1_out));  // open: en
  Register #(.width(32)) register_3 (
    .D(adder_3_out), .Q(register_3_q), .clk(and_2_out), .clr(button_1_out));  // open: en
  Register #(.width(32)) register_4 (
    .D(adder_4_out), .Q(register_4_q), .clk(and_2_out), .clr(button_1_out));  // open: en
  Register #(.width(32)) register_5 (
    .D(adder_5_out), .Q(register_5_q), .clk(and_2_out), .clr(button_1_out));  // open: en
  Register #(.width(32)) register_6 (
    .D(adder_6_out), .Q(register_6_q), .clk(and_2_out), .clr(button_1_out));  // open: en
  Register #(.width(32)) register_7 (
    .D(adder_7_out), .Q(register_7_q), .clk(and_2_out), .clr(button_1_out));  // open: en
  Register #(.width(32)) register_8 (
    .D(adder_8_out), .Q(register_8_q), .clk(and_2_out), .clr(button_1_out));  // open: en
  Register #(.width(32)) register_9 (
    .D(adder_9_out), .Q(register_9_q), .clk(and_2_out), .clr(button_1_out));  // open: en
  Register #(.width(32)) register_10 (
    .D(adder_10_out), .Q(register_10_q), .clk(and_2_out), .clr(button_1_out));  // open: en
  RF rf_1 (
    .in_1(1'b1), .in_2(counter_1_q), .out_6(rf_1_out_6), .out_10(rf_1_out_10), .out_14(rf_1_out_14),
    .out_18(rf_1_out_18), .out_22(rf_1_out_22), .out_26(rf_1_out_26), .out_30(rf_1_out_30),
    .out_7(rf_1_out_7), .out_11(rf_1_out_11), .out_15(rf_1_out_15), .out_19(rf_1_out_19),
    .out_23(rf_1_out_23), .out_27(rf_1_out_27), .out_31(rf_1_out_31), .out_8(rf_1_out_8),
    .out_12(rf_1_out_12), .out_16(rf_1_out_16), .out_20(rf_1_out_20), .out_24(rf_1_out_24),
    .out_28(rf_1_out_28), .out_32(rf_1_out_32), .out_9(rf_1_out_9), .out_13(rf_1_out_13),
    .out_17(rf_1_out_17), .out_21(rf_1_out_21), .out_25(rf_1_out_25), .out_29(rf_1_out_29),
    .out_33(rf_1_out_33), .in_4(and_2_out), .in_5(button_1_out), .in_3(rom_1_data));
  Adder #(.width(32)) adder_11 (.a(register_1_q), .b(bit_extender_13_out), .out(adder_11_out));  // open: cin, cout
  assign bit_extender_13_out = {{16{1'b0}}, 16'h27};  // Bit_Extender bit_extender_13
  Adder #(.width(32)) adder_12 (.a(register_2_q), .b(bit_extender_14_out), .out(adder_12_out));  // open: cin, cout
  assign bit_extender_14_out = {{16{1'b0}}, 16'h1b};  // Bit_Extender bit_extender_14
  Adder #(.width(32)) adder_13 (.a(register_3_q), .b(bit_extender_15_out), .out(adder_13_out));  // open: cin, cout
  assign bit_extender_15_out = {{16{1'b1}}, 16'hffe9};  // Bit_Extender bit_extender_15
  Adder #(.width(32)) adder_14 (.a(register_4_q), .b(bit_extender_16_out), .out(adder_14_out));  // open: cin, cout
  assign bit_extender_16_out = {{16{1'b0}}, 16'h4};  // Bit_Extender bit_extender_16
  Adder #(.width(32)) adder_15 (.a(register_5_q), .b(bit_extender_17_out), .out(adder_15_out));  // open: cin, cout
  assign bit_extender_17_out = {{16{1'b1}}, 16'hffdf};  // Bit_Extender bit_extender_17
  Adder #(.width(32)) adder_16 (.a(register_6_q), .b(bit_extender_18_out), .out(adder_16_out));  // open: cin, cout
  assign bit_extender_18_out = {{16{1'b1}}, 16'hffc0};  // Bit_Extender bit_extender_18
  Adder #(.width(32)) adder_17 (.a(register_7_q), .b(bit_extender_19_out), .out(adder_17_out));  // open: cin, cout
  assign bit_extender_19_out = {{16{1'b0}}, 16'h23};  // Bit_Extender bit_extender_19
  Adder #(.width(32)) adder_18 (.a(register_8_q), .b(bit_extender_20_out), .out(adder_18_out));  // open: cin, cout
  assign bit_extender_20_out = {{16{1'b0}}, 16'hf};  // Bit_Extender bit_extender_20
  Adder #(.width(32)) adder_19 (.a(register_9_q), .b(bit_extender_21_out), .out(adder_19_out));  // open: cin, cout
  assign bit_extender_21_out = {{16{1'b0}}, 16'h42};  // Bit_Extender bit_extender_21
  Adder #(.width(32)) adder_20 (.a(register_10_q), .b(bit_extender_22_out), .out(adder_20_out));  // open: cin, cout
  assign bit_extender_22_out = {{16{1'b0}}, 16'hc};  // Bit_Extender bit_extender_22
  DotMatrix #(.inputtype("row"), .matrixcols(28), .matrixrows(28)) dotmatrix_1 (
    .row0(rf_1_out_6), .row1(rf_1_out_7), .row2(rf_1_out_8), .row3(rf_1_out_9), .row4(rf_1_out_10),
    .row5(rf_1_out_11), .row6(rf_1_out_12), .row7(rf_1_out_13), .row8(rf_1_out_14), .row9(rf_1_out_15),
    .row10(rf_1_out_16), .row11(rf_1_out_17), .row12(rf_1_out_18), .row13(rf_1_out_19), .row14(rf_1_out_20),
    .row15(rf_1_out_21), .row16(rf_1_out_22), .row17(rf_1_out_23), .row18(rf_1_out_24), .row19(rf_1_out_25),
    .row20(rf_1_out_26), .row21(rf_1_out_27), .row22(rf_1_out_28), .row23(rf_1_out_29), .row24(rf_1_out_30),
    .row25(rf_1_out_31), .row26(rf_1_out_32), .row27(rf_1_out_33));
  relu relu_1 (.in_1(adder_11_out), .out_2(relu_1_out_2));
  relu relu_2 (.in_1(adder_12_out), .out_2(relu_2_out_2));
  relu relu_3 (.in_1(adder_13_out), .out_2(relu_3_out_2));
  relu relu_4 (.in_1(adder_14_out), .out_2(relu_4_out_2));
  relu relu_5 (.in_1(adder_15_out), .out_2(relu_5_out_2));
  relu relu_6 (.in_1(adder_16_out), .out_2(relu_6_out_2));
  relu relu_7 (.in_1(adder_17_out), .out_2(relu_7_out_2));
  relu relu_8 (.in_1(adder_18_out), .out_2(relu_8_out_2));
  relu relu_9 (.in_1(adder_19_out), .out_2(relu_9_out_2));
  relu relu_10 (.in_1(adder_20_out), .out_2(relu_10_out_2));
  Counter #(.width(4), .max('h1)) counter_4 (
    .count(counter_5_carry), .carry(counter_4_carry), .clk(multiplexer_1_out), .clr(button_1_out));  // open: load, D, Q
  Multiplexer #(.select(4), .width(32), .enable("false")) multiplexer_3 (
    .in0(relu_1_out_2), .in1(relu_2_out_2), .in2(relu_3_out_2), .in3(relu_4_out_2), .in4(relu_5_out_2),
    .in5(relu_6_out_2), .in6(relu_7_out_2), .in7(relu_8_out_2), .in8(relu_9_out_2), .in9(relu_10_out_2),
    .out(multiplexer_3_out), .sel(counter_5_q));  // open: in10, in11, in12, in13, in14, in15
  Counter #(.width(4), .max('h9)) counter_5 (
    .count(d_ff_1_q), .Q(counter_5_q), .carry(counter_5_carry), .clk(multiplexer_1_out), .clr(button_1_out));  // open: load, D
  and and_3 (and_3_out, d_ff_1_q, multiplexer_1_out);
  LED led_1 (.in(counter_4_carry));
  Hex_Digit_Display hex_digit_display_3 (.value(multiplexer_4_out));  // open: dp
  Multiplexer #(.width(4), .enable("false")) multiplexer_4 (
    .in0(4'b1110), .in1(max10_1_out_11), .out(multiplexer_4_out), .sel(counter_4_carry));
  Multiplexer #(.width(32), .enable("false")) multiplexer_5 (
    .in0({32{1'b0}}), .in1(multiplexer_3_out), .out(multiplexer_5_out), .sel(d_ff_1_q));
  assign bit_extender_23_out = {{16{rom_12_data[15]}}, rom_12_data};  // Bit_Extender bit_extender_23
  ROM #(.addrWidth(4), .dataWidth(16)) rom_12 (.addr(counter_5_q), .data(rom_12_data));  // open: sel
  ROM #(.addrWidth(4), .dataWidth(16)) rom_13 (.addr(counter_5_q), .data(rom_13_data));  // open: sel
  assign bit_extender_24_out = {{16{rom_13_data[15]}}, rom_13_data};  // Bit_Extender bit_extender_24
  ROM #(.addrWidth(4), .dataWidth(16)) rom_14 (.addr(counter_5_q), .data(rom_14_data));  // open: sel
  assign bit_extender_25_out = {{16{rom_14_data[15]}}, rom_14_data};  // Bit_Extender bit_extender_25
  ROM #(.addrWidth(4), .dataWidth(16)) rom_15 (.addr(counter_5_q), .data(rom_15_data));  // open: sel
  assign bit_extender_26_out = {{16{rom_15_data[15]}}, rom_15_data};  // Bit_Extender bit_extender_26
  ROM #(.addrWidth(4), .dataWidth(16)) rom_16 (.addr(counter_5_q), .data(rom_16_data));  // open: sel
  assign bit_extender_27_out = {{16{rom_16_data[15]}}, rom_16_data};  // Bit_Extender bit_extender_27
  ROM #(.addrWidth(4), .dataWidth(16)) rom_17 (.addr(counter_5_q), .data(rom_17_data));  // open: sel
  assign bit_extender_28_out = {{16{rom_17_data[15]}}, rom_17_data};  // Bit_Extender bit_extender_28
  assign bit_extender_29_out = {{16{rom_18_data[15]}}, rom_18_data};  // Bit_Extender bit_extender_29
  ROM #(.addrWidth(4), .dataWidth(16)) rom_18 (.addr(counter_5_q), .data(rom_18_data));  // open: sel
  ROM #(.addrWidth(4), .dataWidth(16)) rom_19 (.addr(counter_5_q), .data(rom_19_data));  // open: sel
  assign bit_extender_30_out = {{16{rom_19_data[15]}}, rom_19_data};  // Bit_Extender bit_extender_30
  ROM #(.addrWidth(4), .dataWidth(16)) rom_20 (.addr(counter_5_q), .data(rom_20_data));  // open: sel
  assign bit_extender_31_out = {{16{rom_20_data[15]}}, rom_20_data};  // Bit_Extender bit_extender_31
  ROM #(.addrWidth(4), .dataWidth(16)) rom_21 (.addr(counter_5_q), .data(rom_21_data));  // open: sel
  assign bit_extender_32_out = {{16{rom_21_data[15]}}, rom_21_data};  // Bit_Extender bit_extender_32
  Multiplier #(.width(32)) multiplier_11 (
    .a(multiplexer_5_out), .b(bit_extender_23_out), .out(multiplier_11_out));  // open: cin, cout
  Multiplier #(.width(32)) multiplier_12 (
    .a(multiplexer_5_out), .b(bit_extender_24_out), .out(multiplier_12_out));  // open: cin, cout
  Multiplier #(.width(32)) multiplier_13 (
    .a(multiplexer_5_out), .b(bit_extender_25_out), .out(multiplier_13_out));  // open: cin, cout
  Multiplier #(.width(32)) multiplier_14 (
    .a(multiplexer_5_out), .b(bit_extender_26_out), .out(multiplier_14_out));  // open: cin, cout
  Multiplier #(.width(32)) multiplier_15 (
    .a(multiplexer_5_out), .b(bit_extender_27_out), .out(multiplier_15_out));  // open: cin, cout
  Multiplier #(.width(32)) multiplier_16 (
    .a(multiplexer_5_out), .b(bit_extender_28_out), .out(multiplier_16_out));  // open: cin, cout
  Multiplier #(.width(32)) multiplier_17 (
    .a(multiplexer_5_out), .b(bit_extender_29_out), .out(multiplier_17_out));  // open: cin, cout
  Multiplier #(.width(32)) multiplier_18 (
    .a(multiplexer_5_out), .b(bit_extender_30_out), .out(multiplier_18_out));  // open: cin, cout
  Multiplier #(.width(32)) multiplier_19 (
    .a(multiplexer_5_out), .b(bit_extender_31_out), .out(multiplier_19_out));  // open: cin, cout
  Multiplier #(.width(32)) multiplier_20 (
    .a(multiplexer_5_out), .b(bit_extender_32_out), .out(multiplier_20_out));  // open: cin, cout
  Adder #(.width(32)) adder_21 (.a(multiplier_11_out), .b(register_11_q), .out(adder_21_out));  // open: cin, cout
  Adder #(.width(32)) adder_22 (.a(multiplier_12_out), .b(register_12_q), .out(adder_22_out));  // open: cin, cout
  Adder #(.width(32)) adder_23 (.a(multiplier_13_out), .b(register_13_q), .out(adder_23_out));  // open: cin, cout
  Adder #(.width(32)) adder_24 (.a(multiplier_14_out), .b(register_14_q), .out(adder_24_out));  // open: cin, cout
  Adder #(.width(32)) adder_25 (.a(multiplier_15_out), .b(register_15_q), .out(adder_25_out));  // open: cin, cout
  Adder #(.width(32)) adder_26 (.a(multiplier_16_out), .b(register_16_q), .out(adder_26_out));  // open: cin, cout
  Adder #(.width(32)) adder_27 (.a(multiplier_17_out), .b(register_17_q), .out(adder_27_out));  // open: cin, cout
  Adder #(.width(32)) adder_28 (.a(multiplier_18_out), .b(register_18_q), .out(adder_28_out));  // open: cin, cout
  Adder #(.width(32)) adder_29 (.a(multiplier_19_out), .b(register_19_q), .out(adder_29_out));  // open: cin, cout
  Adder #(.width(32)) adder_30 (.a(multiplier_20_out), .b(register_20_q), .out(adder_30_out));  // open: cin, cout
  Register #(.width(32)) register_11 (
    .D(adder_21_out), .Q(register_11_q), .clk(and_3_out), .clr(button_1_out));  // open: en
  Register #(.width(32)) register_12 (
    .D(adder_22_out), .Q(register_12_q), .clk(and_3_out), .clr(button_1_out));  // open: en
  Register #(.width(32)) register_13 (
    .D(adder_23_out), .Q(register_13_q), .clk(and_3_out), .clr(button_1_out));  // open: en
  Register #(.width(32)) register_14 (
    .D(adder_24_out), .Q(register_14_q), .clk(and_3_out), .clr(button_1_out));  // open: en
  Register #(.width(32)) register_15 (
    .D(adder_25_out), .Q(register_15_q), .clk(and_3_out), .clr(button_1_out));  // open: en
  Register #(.width(32)) register_16 (
    .D(adder_26_out), .Q(register_16_q), .clk(and_3_out), .clr(button_1_out));  // open: en
  Register #(.width(32)) register_17 (
    .D(adder_27_out), .Q(register_17_q), .clk(and_3_out), .clr(button_1_out));  // open: en
  Register #(.width(32)) register_18 (
    .D(adder_28_out), .Q(register_18_q), .clk(and_3_out), .clr(button_1_out));  // open: en
  Register #(.width(32)) register_19 (
    .D(adder_29_out), .Q(register_19_q), .clk(and_3_out), .clr(button_1_out));  // open: en
  Register #(.width(32)) register_20 (
    .D(adder_30_out), .Q(register_20_q), .clk(and_3_out), .clr(button_1_out));  // open: en
  assign bit_extender_33_out = {{16{1'b1}}, 16'hffda};  // Bit_Extender bit_extender_33
  assign bit_extender_34_out = {{16{1'b0}}, 16'h29};  // Bit_Extender bit_extender_34
  assign bit_extender_35_out = {{16{1'b0}}, 16'h6};  // Bit_Extender bit_extender_35
  assign bit_extender_36_out = {{16{1'b1}}, 16'hffe2};  // Bit_Extender bit_extender_36
  assign bit_extender_37_out = {{16{1'b0}}, 16'h16};  // Bit_Extender bit_extender_37
  assign bit_extender_38_out = {{16{1'b0}}, 16'h4c};  // Bit_Extender bit_extender_38
  assign bit_extender_39_out = {{16{1'b1}}, 16'hfff4};  // Bit_Extender bit_extender_39
  assign bit_extender_40_out = {{16{1'b0}}, 16'h1f};  // Bit_Extender bit_extender_40
  assign bit_extender_41_out = {{16{1'b1}}, 16'hffa6};  // Bit_Extender bit_extender_41
  assign bit_extender_42_out = {{16{1'b0}}, 16'h1};  // Bit_Extender bit_extender_42
  relu relu_11 (.in_1(adder_31_out), .out_2(relu_11_out_2));
  Adder #(.width(32)) adder_31 (.a(register_11_q), .b(bit_extender_33_out), .out(adder_31_out));  // open: cin, cout
  Adder #(.width(32)) adder_32 (.a(register_12_q), .b(bit_extender_34_out), .out(adder_32_out));  // open: cin, cout
  relu relu_12 (.in_1(adder_32_out), .out_2(relu_12_out_2));
  relu relu_13 (.in_1(adder_33_out), .out_2(relu_13_out_2));
  Adder #(.width(32)) adder_33 (.a(register_13_q), .b(bit_extender_35_out), .out(adder_33_out));  // open: cin, cout
  Adder #(.width(32)) adder_34 (.a(register_14_q), .b(bit_extender_36_out), .out(adder_34_out));  // open: cin, cout
  relu relu_14 (.in_1(adder_34_out), .out_2(relu_14_out_2));
  relu relu_15 (.in_1(adder_35_out), .out_2(relu_15_out_2));
  Adder #(.width(32)) adder_35 (.a(register_15_q), .b(bit_extender_37_out), .out(adder_35_out));  // open: cin, cout
  relu relu_16 (.in_1(adder_36_out), .out_2(relu_16_out_2));
  Adder #(.width(32)) adder_36 (.a(register_16_q), .b(bit_extender_38_out), .out(adder_36_out));  // open: cin, cout
  relu relu_17 (.in_1(adder_37_out), .out_2(relu_17_out_2));
  Adder #(.width(32)) adder_37 (.a(register_17_q), .b(bit_extender_39_out), .out(adder_37_out));  // open: cin, cout
  relu relu_18 (.in_1(adder_38_out), .out_2(relu_18_out_2));
  Adder #(.width(32)) adder_38 (.a(register_18_q), .b(bit_extender_40_out), .out(adder_38_out));  // open: cin, cout
  Adder #(.width(32)) adder_39 (.a(register_19_q), .b(bit_extender_41_out), .out(adder_39_out));  // open: cin, cout
  relu relu_19 (.in_1(adder_39_out), .out_2(relu_19_out_2));
  relu relu_20 (.in_1(adder_40_out), .out_2(relu_20_out_2));
  Adder #(.width(32)) adder_40 (.a(register_20_q), .b(bit_extender_42_out), .out(adder_40_out));  // open: cin, cout
  max10 max10_1 (
    .in_1(relu_11_out_2), .in_2(relu_12_out_2), .in_3(relu_13_out_2), .in_4(relu_14_out_2),
    .in_5(relu_15_out_2), .in_6(relu_16_out_2), .in_7(relu_17_out_2), .in_8(relu_18_out_2),
    .in_9(relu_19_out_2), .in_10(relu_20_out_2), .out_11(max10_1_out_11));

  // Notes on the sheet:
  //   contents of rom_1 (hex, n*v repeats v):
  //   4*0 30 70 e0 e0 40c0 c180 c180 1c380 18700 38600 78e00 ffc00 1cfe00 307e00 6000 e000 c000 1c000
  //   38000 10000
  //   contents of rom_2 (hex, n*v repeats v):
  //   7 6 6 fff9 fff9 3 ffff 3 5 5 1 1 fffd fff9 c ffff fffc 3 fffe 0 2 fffe 4 ffff 3 fffb fffc 6 8 fff8 1
  //   fffa ffff 6 fff6 1f 16 ffee ffdf ffd1 ffec ffe3 fff1 3 12 fff2 ffe8 15 1e d f e 0 5 3 1 8 1 1 8 ffea
  //   ffff 5 27 c 13 fff3 8 18 30 3 1c 3f 27 10 7 fff3 fffe ffe0 fff1 1 1a 6 8 0 ffff 7 0 fffe 22 2a c 17
  //   18 2f fffb 2b 2f 16 14 13 11 18 d 1a 1 ffe9 fff3 fff6 2b 6 7 fff8 4 fff9 4 22 2b 12 fffb 28 6 1d 12
  //   10 5 1c b f 9 f 0 fffc fffb ffee ffee fff8 2 1c 6 ffff 7 fffe 18 fffc 33 5 22 ffed c 15 1 3 0 9 1 e
  //   b 10 4 c 8 a 19 fff3 8 fff1 0 ffff 6 fffd 23 29 11 c 6 fffe 16 8 b 8 2 b 1 b fffa 9 fff9 7 4 fff4 7
  //   30 a 11 18 ffff 1c ffdb 14 1 fffa fff6 fffc b 5 e ffff 6 fffe 12 fff7 7 ffff 1 fffe 9 8 9 fffd b e e
  //   ffef fffa 0 d fff9 2 ffee ffec 1 3 3 d d 0 d 12 fffe fff9 2 fff7 17 e 2 e 9 e 2e 33 3 4 10 15 fffd b
  //   ffec fff8 0 9 e fffb 6 9 fff4 ffff d fffd fff9 fffc fff5 fffb 9 19 f 30 2d 23 17 fffa 6 fff9 a fff8
  //   5 3 fff2 3 fff8 fff8 fff7 ffea fff3 fffb 3 fffe fffa ffe2 ffd8 ffe5 ffe9 ffd7 ffee fff7 31 2b 1a
  //   fff4 fff4 1 fff0 fffa fffa fff5 ffe4 fff0 ffe3 ffe7 ffeb fff1 ffe6 fff7 fffc fffa ffef ffe1 ffdc
  //   ffaf ffa1 ff9c ffac ffae 12 20 ffe7 fff6 fffd ffeb fff6 ffe2 ffe8 ffd7 ffcf ffd6 ffe3 fff7 fff2 fff0
  //   fff4 fffa 4 1 ffe6 fff3 ffea ffea ffd7 ffc0 ff96 ff7e ffea fff7 ffed 4 ffe5 fff2 ffd9 ffd3 ffc2 ffd2
  //   ffd7 ffed ffee ffef fffa 10 11 1d 6 fff5 2 7 0 fff9 fff8 ffe5 ffc7 ffd5 d 16 fff8 1 fffa ffdd 5 ffee
  //   ffde fff4 ffeb fff9 a 4 fffe 6 c 17 7 9 fffc fff9 fffb 2 fff2 ffed fff0 a a 32 fffb fffa 8 fff0 fffa
  //   fffb fffc 1b 1 3 4 fffd 9 f 1d d b a fff5 ffff 1 fff7 ffef fff0 ffe5 23 23 8 22 6 0 32 1a 2e c 6
  //   ffea ffd9 fff7 fffa fffb 7 21 12 fffe fffc 6 0 9 9 1a 22 1 46 50 25 1a fffa e 17 33 33 12 15 fff6
  //   fff2 ffe5 ffe5 ffea fff7 c 10 b 1 b e fffd 14 8 d d 17 2a 46 fff8 1 5 6 3d 29 17 13 6 fff3 ffed ffe0
  //   ffe2 a e f 5 f f 6 19 7 13 1d 24 2d 45 2d 1d 6 9 fff2 26 3d d b 12 f 12 fff8 3 6 14 15 1e 1c 16 14 8
  //   d e 17 7 19 44 31 fffb 2 fff8 13 24 10 17 13 8 12 1c 9 9 fffc fff8 c 2 19 1e 19 11 15 16 24 28 26 1b
  //   1a 3 2 0 26 3e 20 14 9 11 10 ffff e 6 fffe 7 fffc 8 8 1c 19 22 e 21 1d 3b 2a 4a ffec 4 fff9 7 12 5
  //   2d 16 1 ffff 4 7 fffc ffff 0 ffec fffe 3 1 16 24 1e 29 8 1d ffec 9 33 15 fff8 8 5 1d 1 8 e 8 fffd 4
  //   8 6 c 1 ffff fffa 8 0 5 e 10 25 fffa 27 fffb 29 2f 18 4 fffd fffc 8 24 23 5 d 5 fff3 d fff5 e ffff a
  //   b 6 5 24 14 c 9 22 0 ffef 1e 1d 7 fffd fffc fffb fffe 19 f 5 25 fff4 14 f 9 4 b 1 fff0 fff3 fff2 c
  //   ffed fffa fff2 fff3 d 4 26 ffff fff8 fff9 8 1 fffd fffe fff5 fffe 13 a fff1 9 ffea fff6 fff6 ffe9
  //   ffe5 a 5 ffe4 ffcb ffef ffea a c ffe1 ffff fffe 4 fffa 7 fffa ffff 1 4 ffff 3 fffb 8 2 0 ffeb fff5 9
  //   fff5 fff8 ffe1 ffec ffdc d ffdf b ffee 7 7 8 fffb 1
  //   contents of rom_3 (hex, n*v repeats v):
  //   fff8 4 1 fff9 7 2 ffff 1 fffa 1 7 3 7 6 ffff fff9 fff9 fffa fff9 fffa fff9 1 7 fffc 6 7 0 7 7 fff9 3
  //   fffd fffe 3 21 23 1f c a fffc fffc fff4 ffeb fffa fff6 fff8 b 6 11 5 1a 1c 3 fffc 3 1 fffe 3 7 fffb
  //   ffea 2 12 30 26 1e 27 fffb 10 20 24 e ffea 14 17 ffff fff7 fff9 d 29 1b 16 4 7 1 2 fffe fffe 0 fff1
  //   24 25 fff8 9 fff2 fff4 3 0 fff4 fff6 fff0 ffc4 ffda fff7 fff6 fff0 5 4 a a 8 4 4 fffb 7 fffd 4 6 a
  //   ffe4 5 fff3 fffa ffe7 fff0 2 fff0 fff6 fff5 0 ffed ffff fff0 fff6 ffe5 ffd7 ffe0 14 fff5 8 fffa fffe
  //   fffa ffe6 2 24 12 17 9 5 ffff fff8 4 fffd 1 ffff ffff fffb ffee ffea fff8 3 c fff1 fff8 fff7 13 fffc
  //   2 5 ffec ffe9 3 16 21 1c 3 e a b a 0 fff3 fff8 fffb fffe fff5 fff4 ffef 8 fffe 8 1 fff1 e 23 2 0 39
  //   5 2a 1c f 28 a c f a 3 ffff ffe7 fff7 fff8 fff9 a 3 11 18 a 1b 8 fff9 2e 9 fffe 18 6 20 32 10 1c 1e
  //   21 10 14 15 20 0 2 9 fff3 fffe 4 2 e fff2 e 21 ffff ffec 1b d 7 17 28 2c 1b 1d 12 f 1a 1 5 4 d 7 10
  //   7 0 6 fffd 5 fffa b b 8 1e 7 2e 2b 7 14 1e fffe 1a 1b 12 3 c f 11 4 3 21 12 0 5 8 4 4 4 16 ffff 1c
  //   21 14 33 c b 24 16 fff5 24 14 7 25 a 1b c 3 fff4 fffb 6 fff8 e fff9 1 3 fffe fffa 9 11 1a 1 ffea
  //   fffc 0 7 fff5 fffc 32 19 6 f 13 2 ffe7 ffee ffd5 ffd2 fffe 1 0 ffeb 6 fff2 fff7 fff2 ffe6 ffec b 21
  //   21 fff7 fffe 1 29 4 ffef ffe5 ffee ffe4 ffea ffed ffda ffca ffc3 ffe7 2 fff9 fff3 fff7 fff1 fff3
  //   fffc fffb 6 c 2b 3b 8 14 fffe 7 1b 4 ffd2 ffeb ffdd ffe3 ffd7 ffc8 ffd8 ffd1 ffd9 5 12 fffd fffe 3 2
  //   17 b fffa 11 11 fff7 12 fffb 1 5 fffe 27 1 ffcc ffd3 ffeb ffd4 ffd9 ffd1 ffd5 ffec 0 1f f 4 fffb 3 5
  //   fff1 fff1 c e fffa 12 fff7 9 e 1 fffe fffc 5 ffdb ffdc ffeb ffd4 ffc9 ffd5 ffe3 fffe f 16 11 7 8
  //   fffb 0 4 fffe 0 5 ffea fff0 fff8 11 ffff fff8 1 fffd ffe8 ffd3 ffec ffd9 ffd3 ffcd fff5 ffff 1b 16
  //   1e 13 ffef 2 fff3 3 0 2 fff4 fff5 e 13 12 29 8 8 2 fffe ffd9 ffe7 ffe0 ffcf ffde ffd4 6 19 17 26 1f
  //   14 b fff4 fff8 2 ffe7 ffec fffd ffec fff5 7 ffdd 4 c 7 ffff ffe6 fffd 8 ffd1 ffe9 fff4 fff7 1c 8 1a
  //   29 14 15 f 6 fff3 ffe5 fff7 2 ffec ffed ffea ffff 9 10 9 ffff fffa ffe2 fff4 fff5 ffc6 fff5 fffd
  //   fffd 9 10 d 25 1a f 4 fff4 fff9 fff1 fff9 ffee ffe8 ffda fffc c fff4 17 5 fff8 fffd 1 d ffed ffed 2
  //   ffeb 3 fffe c d c b 10 f b 9 1 1 fffc 2 ffe1 0 18 2c fff0 fffd fffb 6 ffe4 ffde fffb 2d 4 a 1 fff8
  //   fffa fffb 2 7 c 13 3 12 4 d fff8 8 ffda ffba 1e 24 a fff8 3 fff9 fff9 ffce ffe9 2 21 2 ffeb e 1 8 b
  //   c 8 17 f a 7 2 ffe9 ffe2 b fff6 ffdd 10 23 0 fffe 6 fffd ffee ffdb 6 fff2 ffef fff5 fffb ffff fffd e
  //   b b 2 4 fffc 9 6 3 0 fff7 ffbc 7 ffe3 fffb 1 fffe 1 4 20 fff6 fff1 fff1 fff0 fff7 fff4 ffeb 1 fffc
  //   fff7 fffc 6 fffc 7 3 fff8 ffe0 ffeb 0 ffda fff0 3 3 2 3 ffff fff9 fffb ffe0 ffed fff1 fff6 fffb 1
  //   fffa 1 fffb fff0 e 2 fff7 d fff5 b 2 fff5 fffc ffe5 2 fff9 fff9 fffd 1 7 7 fffe fff8 e e d f 27 28
  //   ffed fffc 44 e b 17 50 6 10 e 7 ffe7 2 fffb 2 8
  //   contents of rom_4 (hex, n*v repeats v):
  //   fff8 3 0 2 fffa fffb fff7 7 7 4 2 fffe 3 fff8 b 4 3 7 2 7 fffe 1 4 fffd fffb fffd 3 7 fffc 2 fffc
  //   fff9 3 fff8 fff4 fff3 6 fff5 ffec ffdd ffd9 ffd5 9 1c b 7 fff1 ffec ffdd fff7 ffe9 fff2 7 3 8 fffd 3
  //   fff8 2 2 ffed fffe 1 ffea 14 fff6 ffeb 11 1d 1d 7 21 4 6 ffdd ffe0 5 2 ffd9 3 9 9 1 fff9 7 fff8 fffb
  //   4 fff9 ffee fff0 ffec ffec 8 ffe9 fffd ffd7 fff5 ffec ffea fff7 ffef ffe2 ffe4 ffdf fffb e fff7 ffeb
  //   ffd6 7 fffd 1 fffc 1 6 ffd6 ffe1 11 fff6 9 c 1 fff0 1 12 fffe 3 b 3 fff5 0 9 fff5 ffff fff4 ffba
  //   ffd4 ffea fffd fff8 fffb 4 ffe5 14 3 fff9 4 fffb fff0 fff3 fffd fffe 0 a 9 fff8 fffe fffd 4 fff6 2 6
  //   fffa fff9 ffde ffec 4 8 fffd ffe6 ffe0 ffe3 fff5 fff6 ffed fff3 fff5 9 fffe fffe 2 1 ffff 3 fffe
  //   fff9 fff2 fffd fff7 fff0 0 ffda ffea ffdc ffed fffd ffe3 8 ffc5 f ffef ffdf ffea fff6 ffee fff7 fffb
  //   fff2 fff7 a 0 4 fffe fffb 1 fffa fffd ffee ffec ffc7 ffe9 1 a 7 ffe6 ffe9 ffed ffef ffef fff4 0 fffb
  //   ffff fff4 fff1 ffff 4 11 14 1 ffff fffc fffa fff2 fff7 fff0 ffd1 ffbc ffdc ffea 2 0 ffe2 ffda ffe1
  //   fff1 fff4 ffea fff9 fffb fff0 1 2 2 b 4 18 f 4 d fff5 fff4 ffec ffe9 ffce ffb9 ffcf ffe0 fff0 7 fffb
  //   ffde ffe9 ffef fff8 fffc fff1 1 2 fffc 6 4 d 15 1c 10 17 f f fff2 ffde ffd7 ff9b ffa8 ffc2 ffdb 16 2
  //   fff3 ffda fff1 fff1 fffb fff2 2 fffe 4 e b 12 a f 21 16 11 d 11 0 fff6 ffe2 ffb6 ffbe ffd3 d fffa 7
  //   ffe6 ffdc ffff 3 e c 4 4 7 fffe 3 2 f 21 1a 1d 18 1b 14 ffec ffe3 ffe1 fff0 fffa 4 fff8 0 fff8 2
  //   ffdd fffc fff3 fffa 2 fff9 fff2 fffe fffd ffff d 5 17 25 14 24 16 fff9 ffe4 ffd5 ffde fff0 fff2 7 49
  //   f fff9 ffe5 3 fff2 6 fff9 fff9 fffc 2 fffe ffea 3 b c 18 1b 13 10 0 ffec ffc8 ffd9 ffdd ffef b 19 12
  //   8 8 fff6 fff9 f 17 ffff fff4 fffa 3 4 fffe 9 fffd e 1b 18 17 fffe ffdf ffd7 ffd0 ffe1 ffeb fff9 ffe2
  //   2c 43 1a fffb 3 f ffff fff1 fffc ffe8 1 fffe f 10 1 6 9 21 e ffff ffef ffe4 ffdb ffed fff3 fff4 ffff
  //   c 19 62 1a fffa fff7 17 12 ffdf ffec ffd7 fff0 9 5 e 6 e c f 1 fff3 ffe5 ffe3 ffee fff1 fffc 8 fff8
  //   fffc 12 3c fffd ffff fffa 6 11 fffd fff3 ffd4 fff9 13 1a 5 6 0 b a ffee fff0 ffea fff8 fff3 10 2 10
  //   15 17 f 26 18 5 fff2 4 a c ffd6 ffee fffc fffd fffd 0 4 fff0 b 1 fffb 8 2 2 c 2 6 4 e ffee 16 3c
  //   fff9 5 f fffe fff8 11 ffe0 fff6 5 2 0 3 0 2 fffa fffe 6 b 16 d 9 8 5 0 1 12 fff8 2c fffb 5 3 ffec 3
  //   fff7 2 fff1 fffa fff9 a fffd ffff fff6 fff6 fffe fff9 4 5 11 b 9 17 5 17 1a 15 fff9 fffc fffa 2 ffde
  //   1a ffef 24 22 fffb fff5 fffa 4 fffc ffe2 fff0 1 fffb fffd f 12 b d f 4 14 19 22 10 fffd 3 ffff fffa
  //   fff0 ffe9 ffed fff0 7 6 fffa fff3 fffe 3 1 fff7 0 d 15 f 1e 5 11 c fff4 ffeb ffee 25 fff8 4 3 fffe
  //   ffc4 ffda ffe2 fff5 fff6 fffd fff7 4 4 fffa fff8 fff9 fffb fffd fffe 15 f 7 2 1d d fff6 1f fffd 8
  //   fffd fffd 5 fff0 a ffe6 ffec ffeb ffe1 ffd8 ffd5 ffde ffd9 ffe5 fffc ffe5 ffef ffdb ffe9 ffd8 ffef 4
  //   fff4 fff1 ffd8 fff9 fffa fff8 6 4 fff8 fffd 20 2 ffe7 fff8 ffeb ffeb fff5 ffed ffe3 ffc0 ffd8 ffd7
  //   ffd9 ffe6 fff2 ffd9 ffec ffed fff3 10 fffe 0 7 3 fffd fffd fff8 fffc fffd 4 fff5 ffea ffdf ffe9 ffd0
  //   b a fff1 c 9 5 fff6 3 fff6 fffd ffe8 e fff9 5 1 fffe fffe
  //   contents of rom_5 (hex, n*v repeats v):
  //   fffc fff9 1 fffc 3 7 ffff 2 fffb 1 fff9 fff9 7 4 fffa fffd fff9 7 fffb fffa fff7 fffe fff7 6 fffd
  //   fffd 7 3 0 fffd 7 8 1 5 fffd fff5 5 fff1 2 5 fff4 3 ffe3 ffe2 ffca 1 0 5 fffb ffef fff0 fff5 4 fffe
  //   fffe 2 ffff 1 fffe fffd 1c ffff fff4 ffde 2 ffe0 ffe9 ffee ffec b ffc9 ffe4 ffc7 ffd4 fff0 5 ffbd
  //   ffc5 ffdd ffd0 ffd6 ffe8 fffa fff8 ffff 1 fff8 fff9 2 fff6 13 11 ffee ffc8 ffc3 ffcc ffd5 ffd7 ffe7
  //   ffed fffe ffe4 fff0 fff6 fff5 c 9 fffa ffda 13 fffd 8 fffd fffd fffb 1 3 ffec 3 13 fff6 fff8 0 10 14
  //   16 10 10 18 c 17 7 2 16 fffc 8 20 17 37 ffff fffa fff9 2 fff0 ffce fff0 fff0 c 6 4 fffb fffb b 1 8 c
  //   18 15 5 14 14 c c d 15 1b ffef fffd 4 ffff c ffed fff0 17 fffc 5 5 fff9 fff7 fff8 0 fff7 fffb fff5
  //   fff3 fffe ffea 3 fffe 3 ffff 27 3c 4f 1e fffd ffff 16 ffca ffde d 19 fff1 0 18 1 8 fff7 fff2 fff0
  //   ffed fff5 fff1 fffa fff9 fffa fffc 9 ffff 1a 2a 44 2b 11 ffef ffda c 16 fff4 0 8 11 fffe 7 fffb fffe
  //   9 3 ffed ffec fff8 fff3 6 2 8 12 fffb e 45 74 4e 23 fff9 ffdb 13 ffe5 fffa fffc 4 12 17 b fffe 7
  //   fffb 1 ffe7 ffe9 ffe9 fff7 fff5 4 5 f 17 1f 2b 86 15 ffe3 1 fffb fffe fff2 10 ffec ffe8 4 8 14 11 7
  //   f 11 2 fffb fff2 fff5 fffc fffd fffb b 4 12 31 34 d 21 fff8 ffe4 fff6 ffe2 8 7 a 1 16 18 12 e 21 2d
  //   19 b a fff2 fff5 ffff ffe2 ffe4 ffee 12 3f 3c 53 7 fff7 ffea fffc ffe6 fffa fffc f 1e c 9 16 16 20
  //   36 21 1f b ffff fff3 fffe ffff fffc ffe9 17 1f 1b fff7 fffa 7 ffec ffd2 ffd4 ffeb 9 b 8 11 7 7 7 2f
  //   20 1a 24 3 3 fffa a fff2 fffa 5 4 ffe6 ffde ffff ffda fff9 ffe7 ffdf ffc7 fff2 ffff fffe fff7 fff7 3
  //   a d 1b 1e 1c 1e e 5 ffee ffea ffe3 fff6 fff8 ffd0 17 ffee ffcd fffa fffe 16 a ffea ffe0 ffda ffe7
  //   ffec fffb 3 fff4 6 14 25 30 11 c fffa fff4 fff9 ffef ffeb ffdc 5 ffe6 fffe ffec fff3 8 2 17 ffde
  //   ffca ffcd ffe7 ffdc ffef ffee ffef 3 14 12 20 b fffe ffec fff4 ffef ffe2 ffe6 fffa 1 a ffe0 ffcc
  //   ffe7 5 fffc ffdd fff8 ffe8 ffea fff9 ffed fff0 ffff fffb fffc 0 12 9 fff7 fffa fffe ffef fffa ffef
  //   fffa fff5 fff0 e ffa7 ffcb fffc 5 2 ffe2 fffe fff6 b 5 fff5 c fffb fff8 fffd 5 9 8 fff9 fffc fff2
  //   ffef 3 d fff9 1e 12 fffe ffb9 1b fffb 1 fffd fffe ffe1 fffb c 6 fff4 fffe 4 2 fffe fff5 fffb fffa 7
  //   8 fffa f fffe fff7 fffb 10 12 3 ffc0 ffdb 6 fffc 7 ffd0 ffd8 0 fffa d 7 8 4 1 fffe fff7 0 ffff b a c
  //   e 1 d 12 1d 24 ffc5 ffe3 ffea 1 6 3 ffea fffc ffe2 b 12 5 9 5 fff5 fffd fffb 10 8 e 4 11 f 1 1a d 10
  //   e ffd4 ffba 9 3 1 1 4 fff2 fffd fff2 1 c ffed fff5 fffe 7 7 8 e d 5 13 13 15 2 b fff4 7 ffdb ffc6 2
  //   fff8 8 3 1c fff6 12 2 fff5 fff5 6 c 8 14 e 18 e 15 23 15 b 1f 7 ffff ffd5 12 ffdb ffdb ffe9 fffb 3
  //   fffc 11 fff7 ffef ffe0 1 fffb f 17 13 23 1a 12 1d 20 1d a 27 21 fff8 fff4 1 1c fffb ffda 6 7 1 fffa
  //   fffe 1d fff3 ffd2 7 ffea 2 fffa 14 3 5 11 fffd fff8 fffa 0 0 fffa 7 ffef 24 22 23 fff8 6 7 fffc fffd
  //   ffff fffa fff5 ffe1 ffd4 ffc2 ffc1 fff8 ffd8 ffea ffee ffdd ffdb fffd ffe2 ffe5 fff7 ffd1 fff2 ffe7
  //   fff9 fffa ffff 1 fffb fffd fffa 6 4 fffa fffa 1 fff7 ffe5 ffe5 ffd6 ffcc fff8 ffe3 ffdb ffda ffdd
  //   fffd ffcf ffb4 ffe2 ffe1 ffe0 fffd 3 fffa 4 9 fffa
  //   contents of rom_6 (hex, n*v repeats v):
  //   3 ffff fffe 4 fffe ffff 6 fffd fffa 5 3 fffc 6 fffa 18 4 7 2 2 6 5 fffe 4 fff9 fff9 ffff fffc fffd 2
  //   fffb 8 8 fffa ffff ffdd ffd6 ffef ffed ffda ffcf ffd3 ffce ffe8 fff1 b ffe8 ffda ffd6 ffdb ffe5 fff1
  //   ffe7 8 2 fffc 4 5 ffff 5 fff8 ffdf 1 ffdf ffdd ffd7 6 ffc5 fff4 fff4 ffd7 fff1 ffd7 fff7 ffd3 ffe9
  //   ffc8 ffeb ffeb ffe4 ffe0 8 21 5 fffe fffd 0 ffff 5 6 3b ffdb fff2 fff9 fffc 0 13 2 fff2 6 fffa fffc
  //   8 fffa ffe9 fff6 fff4 fff9 3 ffe0 18 3 7 6 ffff fff8 1 fff9 2c 20 c 0 8 1e 8 18 6 12 f a 8 d 2 6
  //   fffc fffd ffe4 8 16 3 fffe fffa 1 2 24 15 fff1 ffe8 19 13 16 12 2a 1a 7 e 8 23 f d a fffc fff6 ffed
  //   fff6 fff3 17 ffe6 0 7 fffe fff4 22 2 b 2e b 20 d e a f 10 10 15 5 11 ffff ffff fffe fffc ffff 0 ffef
  //   8 fff5 ffe5 1 21 1e 23 1e 29 33 c 22 1b c 6 fffe 13 2 9 c 8 4 d fffe a e e 17 12 fffa 12 fff9 fff6
  //   20 2a 2a 2e 1a 12 16 16 19 10 9 a 4 b d 5 13 10 1d 5 a 1f 2f 1f 4 a 1 3 7 5 19 33 f ffff d 16 2 d 1
  //   3 fff8 fffd 3 f 1d 1f 19 7 16 14 3 21 b fff5 fffd ffdf 8 2c d f 1c c fffe 4 fffe fffa fff9 ffed ffe9
  //   ffee 8 c c 17 1a 13 e ffe5 ffea ffe6 fffc 14 6 fff7 7 3a ffed 4 4 0 1 4 1 fffc fffa ffd7 ffe6 fff4
  //   fffe 3 2 b 14 b 2e fff9 ffee ffee fff7 ffe1 fff6 ffef 4 16 ffd8 fffc ffe3 fff3 fff6 fff5 fffe 10 1
  //   ffec ffe5 fff4 0 4 fffa 1e 16 4 d fff7 11 1e 24 ffdd 7 9 fff1 ffff ffd9 ffe1 ffdf fffd 7 6 17 12
  //   fff5 fffe fffe 3 8 fffe 10 9 11 ffff fff4 fff4 2 36 52 2c fffa fff4 3 ffed 7 fffb f 1a 6 7 3 7 a
  //   ffff 5 fffc 0 1e 22 26 a c fff0 ffe4 fff9 b 12 ffff 1 ffea 10 12 2f 5 d 12 ffff 3 a 4 5 9 2 d d 21
  //   19 23 0 fffe 15 1 fff8 7 3c 17 6 fffc 1d 11 a 9 6 28 c d 7 fff6 c 11 6 a 15 27 22 5 19 e 8 18 7 0 34
  //   16 fffc a 3b 1b 15 fff0 c 7 d fffd fff2 0 13 e fffe e 1c 22 e e 10 a 5 ffff fff2 18 15 6 ffff 5 1f
  //   fffe 16 1a 12 f fff8 fffc fff9 4 fffd fffe 8 11 21 14 ffff 16 e 3 f fff8 d fffc fff9 21 1 2 ffec 7
  //   1a 32 c fffc 0 fff3 fff0 ffe6 fff9 fffd 0 fffc fffc f 3 fff5 fffb e 4 4 fffb 18 14 3 1 1c fff6 e 16
  //   22 17 8 fffd ffff fff3 fff3 fff4 fffc ffff a fffc 7 fffd fffd d d 4 fff8 ffff ffe7 fff1 8 1 e 3f
  //   fff8 16 7 5 ffee fff3 fffe ffec fffc fff4 fff6 fff3 fffb 0 1 1 12 ffff ffff a 16 ffe5 ffee ffe0 6 1
  //   fff9 2c c fff8 ffce fffe 8 fffe 4 fffd c 2 c fff8 0 c fffb ffff 19 4 fff9 7 f ffde ffef fff5 fff7
  //   fffc fffb 19 1d d ffdf fff9 2 a a 10 f 9 f e fffc 10 b 17 9 10 19 e fff7 fffe fffd ffe3 ffff 1 0 6
  //   19 4 11 14 15 10 13 16 2c 1e 23 24 6 20 6 b ffe5 fff2 11 17 ffc7 a 23 1 2 3 fffe 0 ffdb ffe7 ffef 20
  //   2f fff6 17 2f 1e 9 20 b 25 11 fff5 fff2 fff8 ffd9 ffba ffdd ffd0 ffda 5 6 fff8 fffa 8 4 8 ffe4 ffd2
  //   ffe9 fff2 ffd8 ffb2 ffe7 ffd1 ffff ffde ffdb ffc9 ffd9 ffc6 ffeb ffcd ffb8 ffba ffc2 ffde 5 fffb
  //   ffff 5 3 1 0 fff9 7 fffa 6 ffd5 ffe1 ffef ffe4 ffe8 ffd0 d ffe0 ffcc ffea fffc d ffd7 fff9 fff7 ffde
  //   1 fffe fffa fffd ffff
  //   contents of rom_7 (hex, n*v repeats v):
  //   fffb fffc 6 6 5 fff9 5 fffc 7 fff9 1 ffff 0 10 3 fffb fffb 1 1 8 6 0 1 fffd 0 ffff 1 0 fffc 2 9 fffe
  //   fffe ffff 26 27 23 1b 1a 26 31 34 26 30 43 30 1e 20 1f 1a 15 1f fffc 4 fff9 4 7 fffc fffe fffa 2 5
  //   27 37 3c 3d 3b 37 39 2c 30 b 29 c fffd 4 1d 1d 36 31 34 19 5 fffb 5 9 10 8 ffff 21 34 28 33 45 3d 5e
  //   3f 48 24 1a 11 14 26 fffb 0 ffe4 fff0 fff0 ffff ffdc 3 fffc 8 8 fffd fff7 2a 2e 2b 9 21 23 2a 19 14
  //   1b 17 15 f 3 c fffb 7 ffd3 ffd2 ffc6 ffae fffa fff8 0 6 8 fffc 24 2c 1a 7 10 9 0 b 0 17 1e e f 14
  //   fffd fff9 14 fff5 8 ffed ffd4 ffdd fff4 2c 8 6 3 b 2e e fffd c ffff 4 14 e 10 3 22 18 14 21 8 12
  //   fffe b fffb ffed fffa ffe3 9 ffec 10 ffff 21 ffde b 20 d 2 fffb a fffb 7 fffe 16 6 20 22 8 4 2 3
  //   ffeb fffc fff0 ffd6 ffe4 ffe8 23 6 fff4 ffeb ffe8 fff8 22 ffff 1 5 fffe fff9 fffe 0 e 14 13 1d f 9
  //   fff3 fffc fffd 3 1 ffe2 ffcf ffd2 9 12 7 fff9 ffd7 16 32 c fffb a fff7 3 fff4 fffa fff5 3 21 f 0
  //   fffc fff9 5 3 fffa 13 fff3 ffd1 fffb ffeb ffd8 fffe ffdb ffe0 2d c 12 12 f fff1 fff6 fff4 ffea ffeb
  //   4 17 fff9 4 7 d e c fffb 10 2 ffdd ffb7 ffd8 2 ffe0 ffdc ffe5 17 15 16 ffea ffef 3 ffe9 ffea fff2
  //   fffa 17 1d 0 fff7 2 7 17 28 14 32 d b fff5 ffc9 16 ffec ffed ffd5 ffdf ffef 12 ffef fffd ffec ffff
  //   fff3 ffe7 fffe 11 1d 9 fff7 a 15 9 8 e 1d 1c 37 6 2a 1e 4 ffe3 ffdc 8 fff6 ffef fffb ffed ffed fffd
  //   ffe9 ffe8 ffff 24 16 10 10 c fffe 6 ffe7 fff3 fff9 28 24 4 ffca 5 fffa 0 ffdf 19 ffca ffed fffb ffe5
  //   fffb ffee fff4 fff3 8 1a 13 1b 2 fff9 fff9 fff1 ffeb 1 ffe3 fff6 ffff fff6 29 fff8 fffb 11 ffde fff1
  //   ffff 7 fffe fff8 ffec fff4 ffec fff9 e 1f 18 fffa 3 fff9 fff1 fff1 fff2 fff5 ffeb fff5 1f 2d fff1 12
  //   0 fff9 2e 6 15 fff8 fff2 fffa ffe7 4 8 a 15 f c fff9 fff6 fffa fffa 0 fffb fffb ffff f 1d 2b 12 ffff
  //   9 18 10 22 19 9 ffed 2 0 0 f f 15 fffd fff2 ffea fff1 fffc fff8 5 fff2 fff3 d 10 fff7 15 3f 7 1 13
  //   10 a fff2 ffe7 fffa fff9 fff9 13 1a 9 5 fff5 ffe8 fffb c c 13 12 fff3 1 14 28 ffff 3a c 14 ffff 12
  //   ffd4 fffc fff0 fff9 fff9 8 7 14 1b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
  //   contents of rom_8 (hex, n*v repeats v):
  //   3 8 fff8 fffc fffd 8 1 fffb 4 fffb fff9 fffc 5 3 fff0 ffff 7 1 fffd 2 fffd 5 3 9 ffff 3 ffff fffc
  //   fffe 6 2 2 fffa fffa 20 2e 15 16 1f 24 30 30 0 fff9 fff5 16 1c 1c 1b f 10 e 6 5 4 8 6 2 fffa 4 18 4
  //   20 20 1e fff7 29 fff2 4 fff7 10 2 fff9 6 fff1 27 1c 9 2f 27 fffe ffe8 ffff 3 7 fffe 0 fffa fffe ffff
  //   f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
  //   contents of rom_9 (hex, n*v repeats v):
  //   3 fffd 0 8 fffb fffc 7 ffff 8 3 fffe fffe ffff 11 12 6 fffa 2 8 ffff fffe 6 1 fff8 8 fff8 7 fffe
  //   fffd 1 ffff 1 5 fffe 20 25 27 9 ffff fff1 26 fff6 a 14 3f 4 10 22 1e e 1f 20 1 8 1 5 4 fffc 3 fffd
  //   ffeb fff8 17 33 20 25 31 a 12 fff8 2 fff0 c b 34 fffc 25 1f fffd 14 18 21 fffa fffb 7 4 fffe 6 4
  //   ffe3 ff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
  //   contents of rom_10 (hex, n*v repeats v):
  //   fffc 8 fff8 1 fffd fffb ffff fffc fffd 6 8 8 1 fff9 fffa 9 7 fff8 1 7 fffe ffff 6 3 2 fffc 3 fffc
  //   ffff fff8 fffa 4 5 fffb fff8 ffe2 ffee fff1 fff7 ffe0 ffdb ffe5 3 8 fff3 ffd7 fff6 ffe1 ffe1 ffeb
  //   fff1 fff3 1 fffd fffd fff8 9 5 fffb 4 fff9 2 ffee ffdb ffd8 ffb7 ffb3 ffb7 ffd8 fff6 ffce ffcf fff6
  //   fffc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
  //   contents of rom_11 (hex, n*v repeats v):
  //   fffe 2 fff9 1 2 fffb ffff fffd fff8 4 fffd 6 6 4 fff4 ffff fffd 5 4 6 fff8 7 0 fffa fffa ffff 4 7 3
  //   fffb 1 fffd 6 fffe 18 22 10 10 16 28 fff5 2a fffa fffd ffd7 1c 1a 26 22 11 16 1b 7 fffd 1 fff8 8
  //   fffd fffb fffb 1e 4 22 a 19 a 36 16 12 1 30 16 7 10 12 18 19 13 2e 1c d ffe6 ffff 1 fffb 1 fffd 3 6
  //   ffe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
  //   contents of rom_12 (hex, n*v repeats v):
  //   ff9c ffc2 17 ffc8 31 ffe6 2b 54 2 ff9f
  //   contents of rom_13 (hex, n*v repeats v):
  //   48 23 53 18 ff94 ffff 31 ffbe 5 ffce
  //   contents of rom_14 (hex, n*v repeats v):
  //   22 3e 38 ffc4 44 6 ffcd 27 ffbc ffdd
  //   contents of rom_15 (hex, n*v repeats v):
  //   3e ffbe ffba fffc 24 36 31 ffab 25 ffd3
  //   contents of rom_16 (hex, n*v repeats v):
  //   ffb3 ffc5 46 2c 50 ff8b 24 ffbe ffe9 2e
  //   contents of rom_17 (hex, n*v repeats v):
  //   47 ffbe ff66 36 ffe4 ffc3 fffb 1f 31 ffe8
  //   contents of rom_18 (hex, n*v repeats v):
  //   ffe5 4 fff1 fff0 ffd8 15 32 f ffad 4a
  //   contents of rom_19 (hex, n*v repeats v):
  //   fffb 3a ffeb ffa2 15 ffc0 20 ffad 56 5
  //   contents of rom_20 (hex, n*v repeats v):
  //   ffc9 fff9 b 46 24 fff6 ffa0 1f fff6 fff4
  //   contents of rom_21 (hex, n*v repeats v):
  //   ffb7 ff81 20 ffd9 2 ffdd ff82 ffe8 47 3a
endmodule

module RF (
  input  in_1,
  input  [4:0] in_2,
  input  [27:0] in_3,
  input  in_4,
  input  in_5,
  output [27:0] out_6,
  output [27:0] out_7,
  output [27:0] out_8,
  output [27:0] out_9,
  output [27:0] out_10,
  output [27:0] out_11,
  output [27:0] out_12,
  output [27:0] out_13,
  output [27:0] out_14,
  output [27:0] out_15,
  output [27:0] out_16,
  output [27:0] out_17,
  output [27:0] out_18,
  output [27:0] out_19,
  output [27:0] out_20,
  output [27:0] out_21,
  output [27:0] out_22,
  output [27:0] out_23,
  output [27:0] out_24,
  output [27:0] out_25,
  output [27:0] out_26,
  output [27:0] out_27,
  output [27:0] out_28,
  output [27:0] out_29,
  output [27:0] out_30,
  output [27:0] out_31,
  output [27:0] out_32,
  output [27:0] out_33
);

  wire and_1_out, and_2_out, and_3_out, and_4_out, and_5_out, and_6_out, and_7_out, and_8_out, and_9_out,
       and_10_out, and_11_out, and_12_out, and_13_out, and_14_out, and_15_out, and_16_out, and_17_out,
       and_18_out, and_19_out, and_20_out, and_21_out, and_22_out, and_23_out, and_24_out, and_25_out,
       and_26_out, and_27_out, and_28_out, decoder_1_out0, decoder_1_out1, decoder_1_out2, decoder_1_out3,
       decoder_1_out4, decoder_1_out5, decoder_1_out6, decoder_1_out7, decoder_1_out8, decoder_1_out9,
       decoder_1_out10, decoder_1_out11, decoder_1_out12, decoder_1_out13, decoder_1_out14, decoder_1_out15,
       decoder_1_out16, decoder_1_out17, decoder_1_out18, decoder_1_out19, decoder_1_out20, decoder_1_out21,
       decoder_1_out22, decoder_1_out23, decoder_1_out24, decoder_1_out25, decoder_1_out26, decoder_1_out27;

  Decoder #(.select(5), .enable("false")) decoder_1 (
    .out0(decoder_1_out0), .out1(decoder_1_out1), .out2(decoder_1_out2), .out3(decoder_1_out3),
    .out4(decoder_1_out4), .out5(decoder_1_out5), .out6(decoder_1_out6), .out7(decoder_1_out7),
    .out8(decoder_1_out8), .out9(decoder_1_out9), .out10(decoder_1_out10), .out11(decoder_1_out11),
    .out12(decoder_1_out12), .out13(decoder_1_out13), .out14(decoder_1_out14), .out15(decoder_1_out15),
    .out16(decoder_1_out16), .out17(decoder_1_out17), .out18(decoder_1_out18), .out19(decoder_1_out19),
    .out20(decoder_1_out20), .out21(decoder_1_out21), .out22(decoder_1_out22), .out23(decoder_1_out23),
    .out24(decoder_1_out24), .out25(decoder_1_out25), .out26(decoder_1_out26), .out27(decoder_1_out27),
    .sel(in_2));  // open: out28, out29, out30, out31
  and and_1 (and_1_out, decoder_1_out0, in_1);
  and and_2 (and_2_out, decoder_1_out1, in_1);
  and and_3 (and_3_out, decoder_1_out2, in_1);
  and and_4 (and_4_out, decoder_1_out3, in_1);
  and and_5 (and_5_out, decoder_1_out4, in_1);
  and and_6 (and_6_out, decoder_1_out5, in_1);
  and and_7 (and_7_out, decoder_1_out6, in_1);
  and and_8 (and_8_out, decoder_1_out7, in_1);
  and and_9 (and_9_out, decoder_1_out8, in_1);
  and and_10 (and_10_out, decoder_1_out9, in_1);
  and and_11 (and_11_out, decoder_1_out10, in_1);
  and and_12 (and_12_out, decoder_1_out11, in_1);
  and and_13 (and_13_out, decoder_1_out12, in_1);
  and and_14 (and_14_out, decoder_1_out13, in_1);
  and and_15 (and_15_out, decoder_1_out14, in_1);
  and and_16 (and_16_out, decoder_1_out15, in_1);
  and and_17 (and_17_out, decoder_1_out16, in_1);
  and and_18 (and_18_out, decoder_1_out17, in_1);
  and and_19 (and_19_out, decoder_1_out18, in_1);
  and and_20 (and_20_out, decoder_1_out19, in_1);
  and and_21 (and_21_out, decoder_1_out20, in_1);
  and and_22 (and_22_out, decoder_1_out21, in_1);
  and and_23 (and_23_out, decoder_1_out22, in_1);
  and and_24 (and_24_out, decoder_1_out23, in_1);
  and and_25 (and_25_out, decoder_1_out24, in_1);
  and and_26 (and_26_out, decoder_1_out25, in_1);
  and and_27 (and_27_out, decoder_1_out26, in_1);
  and and_28 (and_28_out, decoder_1_out27, in_1);
  Register #(.width(28)) register_1 (.D(in_3), .en(and_1_out), .Q(out_6), .clk(in_4), .clr(in_5));
  Register #(.width(28)) register_2 (.D(in_3), .en(and_5_out), .Q(out_10), .clk(in_4), .clr(in_5));
  Register #(.width(28)) register_3 (.D(in_3), .en(and_9_out), .Q(out_14), .clk(in_4), .clr(in_5));
  Register #(.width(28)) register_4 (.D(in_3), .en(and_13_out), .Q(out_18), .clk(in_4), .clr(in_5));
  Register #(.width(28)) register_5 (.D(in_3), .en(and_17_out), .Q(out_22), .clk(in_4), .clr(in_5));
  Register #(.width(28)) register_6 (.D(in_3), .en(and_21_out), .Q(out_26), .clk(in_4), .clr(in_5));
  Register #(.width(28)) register_7 (.D(in_3), .en(and_25_out), .Q(out_30), .clk(in_4), .clr(in_5));
  Register #(.width(28)) register_8 (.D(in_3), .en(and_2_out), .Q(out_7), .clk(in_4), .clr(in_5));
  Register #(.width(28)) register_9 (.D(in_3), .en(and_6_out), .Q(out_11), .clk(in_4), .clr(in_5));
  Register #(.width(28)) register_10 (.D(in_3), .en(and_10_out), .Q(out_15), .clk(in_4), .clr(in_5));
  Register #(.width(28)) register_11 (.D(in_3), .en(and_14_out), .Q(out_19), .clk(in_4), .clr(in_5));
  Register #(.width(28)) register_12 (.D(in_3), .en(and_18_out), .Q(out_23), .clk(in_4), .clr(in_5));
  Register #(.width(28)) register_13 (.D(in_3), .en(and_22_out), .Q(out_27), .clk(in_4), .clr(in_5));
  Register #(.width(28)) register_14 (.D(in_3), .en(and_26_out), .Q(out_31), .clk(in_4), .clr(in_5));
  Register #(.width(28)) register_15 (.D(in_3), .en(and_3_out), .Q(out_8), .clk(in_4), .clr(in_5));
  Register #(.width(28)) register_16 (.D(in_3), .en(and_7_out), .Q(out_12), .clk(in_4), .clr(in_5));
  Register #(.width(28)) register_17 (.D(in_3), .en(and_11_out), .Q(out_16), .clk(in_4), .clr(in_5));
  Register #(.width(28)) register_18 (.D(in_3), .en(and_15_out), .Q(out_20), .clk(in_4), .clr(in_5));
  Register #(.width(28)) register_19 (.D(in_3), .en(and_19_out), .Q(out_24), .clk(in_4), .clr(in_5));
  Register #(.width(28)) register_20 (.D(in_3), .en(and_23_out), .Q(out_28), .clk(in_4), .clr(in_5));
  Register #(.width(28)) register_21 (.D(in_3), .en(and_27_out), .Q(out_32), .clk(in_4), .clr(in_5));
  Register #(.width(28)) register_22 (.D(in_3), .en(and_4_out), .Q(out_9), .clk(in_4), .clr(in_5));
  Register #(.width(28)) register_23 (.D(in_3), .en(and_8_out), .Q(out_13), .clk(in_4), .clr(in_5));
  Register #(.width(28)) register_24 (.D(in_3), .en(and_12_out), .Q(out_17), .clk(in_4), .clr(in_5));
  Register #(.width(28)) register_25 (.D(in_3), .en(and_16_out), .Q(out_21), .clk(in_4), .clr(in_5));
  Register #(.width(28)) register_26 (.D(in_3), .en(and_20_out), .Q(out_25), .clk(in_4), .clr(in_5));
  Register #(.width(28)) register_27 (.D(in_3), .en(and_24_out), .Q(out_29), .clk(in_4), .clr(in_5));
  Register #(.width(28)) register_28 (.D(in_3), .en(and_28_out), .Q(out_33), .clk(in_4), .clr(in_5));
endmodule

module MLP (
);

  wire and_1_out, button_1_out, clk_out, comparator_1_lt, counter_1_carry, counter_3_carry, counter_4_carry,
       counter_5_carry, counter_6_carry, counter_7_carry, counter_8_carry, counter_9_carry, counter_10_carry,
       d_ff_1_q, d_ff_2_q, d_ff_3_q, d_ff_4_q, decoder_1_out0, decoder_1_out1, decoder_1_out2,
       decoder_1_out3, decoder_1_out4, decoder_2_out0, decoder_2_out1, decoder_2_out2, decoder_2_out3,
       decoder_2_out4, decoder_2_out5, decoder_2_out6, decoder_2_out7, decoder_2_out8, decoder_2_out9,
       multiplexer_1_out, multiplexer_3_out, multiplexer_5_out, multiplexer_10_out, multiplexer_11_out;
  wire [2:0] counter_4_q, counter_6_q, counter_8_q, multiplexer_4_out;
  wire [3:0] bit_extender_1_out, counter_9_q, counter_10_q, max10_1_out_11, multiplexer_2_out,
       multiplexer_14_out, multiplexer_17_out;
  wire [9:0] counter_1_q, counter_2_q, counter_3_q;
  wire [9:4] multiplexer_2_out_2;
  wire [15:0] multiplexer_6_out, multiplexer_13_out, rom_2_data, rom_3_data, rom_4_data, rom_5_data,
       rom_6_data, rom_7_data, rom_8_data, rom_9_data, rom_10_data, rom_11_data, rom_12_data, rom_13_data,
       rom_14_data, rom_15_data, rom_16_data, rom_17_data, rom_18_data;
  wire [27:0] rf_1_out_6, rf_1_out_7, rf_1_out_8, rf_1_out_9, rf_1_out_10, rf_1_out_11, rf_1_out_12,
       rf_1_out_13, rf_1_out_14, rf_1_out_15, rf_1_out_16, rf_1_out_17, rf_1_out_18, rf_1_out_19,
       rf_1_out_20, rf_1_out_21, rf_1_out_22, rf_1_out_23, rf_1_out_24, rf_1_out_25, rf_1_out_26,
       rf_1_out_27, rf_1_out_28, rf_1_out_29, rf_1_out_30, rf_1_out_31, rf_1_out_32, rf_1_out_33, rom_1_data;
  wire [31:0] adder_1_out, adder_2_out, adder_3_out, adder_4_out, bit_extender_2_out, bit_extender_3_out,
       bit_extender_4_out, bit_extender_5_out, bit_extender_6_out, multiplexer_7_out, multiplexer_8_out,
       multiplexer_9_out, multiplexer_12_out, multiplexer_15_out, multiplexer_16_out, multiplier_1_out,
       multiplier_2_out, register_1_q, register_2_q, register_3_q, register_4_q, register_5_q, register_6_q,
       register_7_q, register_8_q, register_9_q, register_10_q, register_11_q, register_12_q, register_13_q,
       register_14_q, register_15_q;

  Button button_1 (.out(button_1_out));
  Clock clk (.out(clk_out));
  Multiplexer #(.enable("false")) multiplexer_1 (.in0(clk_out), .in1(1'b0), .out(multiplexer_1_out), .sel(d_ff_4_q));
  and and_1 (and_1_out, counter_3_carry, counter_4_carry);
  Hex_Digit_Display hex_digit_display_1 (.value(bit_extender_1_out));  // open: dp
  assign bit_extender_1_out = {{3{1'b0}}, multiplexer_2_out_2[4]};  // Bit_Extender bit_extender_1
  Multiplexer #(.width(10), .enable("false")) multiplexer_2 (
    .in0(counter_2_q), .in1({10{1'b0}}), .out({multiplexer_2_out_2, multiplexer_2_out}), .sel(d_ff_1_q));
  Counter #(.width(10), .max('h1b)) counter_1 (
    .Q(counter_1_q), .carry(counter_1_carry), .clk(multiplexer_1_out), .clr(button_1_out));  // open: load, D, count
  Counter #(.width(10), .max('h1b)) counter_2 (
    .count(counter_1_carry), .Q(counter_2_q), .clk(multiplexer_1_out), .clr(button_1_out));  // open: load, D, carry
  Counter #(.width(10), .max('h30f)) counter_3 (
    .Q(counter_3_q), .carry(counter_3_carry), .clk(multiplexer_1_out), .clr(button_1_out));  // open: load, D, count
  Counter #(.width(3), .max('h4)) counter_4 (
    .count(counter_3_carry), .Q(counter_4_q), .carry(counter_4_carry), .clk(multiplexer_1_out),
    .clr(button_1_out));  // open: load, D
  Counter #(.width(1), .max('h1)) counter_5 (
    .count(and_1_out), .carry(counter_5_carry), .clk(multiplexer_1_out), .clr(button_1_out));  // open: load, D, Q
  Multiplexer #(.enable("false")) multiplexer_3 (
    .in0(multiplexer_1_out), .in1(1'b0), .out(multiplexer_3_out), .sel(d_ff_1_q));
  Hex_Digit_Display hex_digit_display_2 (.value(multiplexer_2_out));  // open: dp
  Multiplexer #(.width(3), .enable("false")) multiplexer_4 (
    .in0(counter_4_q), .in1(counter_6_q), .out(multiplexer_4_out), .sel(d_ff_2_q));
  Decoder #(.select(3), .enable("false")) decoder_1 (
    .out0(decoder_1_out0), .out1(decoder_1_out1), .out2(decoder_1_out2), .out3(decoder_1_out3),
    .out4(decoder_1_out4), .sel(multiplexer_4_out));  // open: out5, out6, out7
  ROM #(.addrWidth(5), .dataWidth(28)) rom_1 (
    .addr({multiplexer_2_out_2[4], multiplexer_2_out}), .data(rom_1_data));  // open: sel
  Multiplexer #(.select(5), .enable("false")) multiplexer_5 (
    .in0(rom_1_data[27]), .in1(rom_1_data[26]), .in2(rom_1_data[25]), .in3(rom_1_data[24]),
    .in4(rom_1_data[23]), .in5(rom_1_data[22]), .in6(rom_1_data[21]), .in7(rom_1_data[20]),
    .in8(rom_1_data[19]), .in9(rom_1_data[18]), .in10(rom_1_data[17]), .in11(rom_1_data[16]),
    .in12(rom_1_data[15]), .in13(rom_1_data[14]), .in14(rom_1_data[13]), .in15(rom_1_data[12]),
    .in16(rom_1_data[11]), .in17(rom_1_data[10]), .in18(rom_1_data[9]), .in19(rom_1_data[8]),
    .in20(rom_1_data[7]), .in21(rom_1_data[6]), .in22(rom_1_data[5]), .in23(rom_1_data[4]),
    .in24(rom_1_data[3]), .in25(rom_1_data[2]), .in26(rom_1_data[1]), .in27(rom_1_data[0]),
    .out(multiplexer_5_out), .sel(counter_1_q[4:0]));  // open: in28, in29, in30, in31
  ROM #(.addrWidth(10), .dataWidth(16)) rom_2 (.addr(counter_3_q), .data(rom_2_data));  // open: sel
  RF rf_1 (
    .in_1(1'b1), .in_2({multiplexer_2_out_2[4], multiplexer_2_out}), .out_6(rf_1_out_6),
    .out_10(rf_1_out_10), .out_14(rf_1_out_14), .out_18(rf_1_out_18), .out_22(rf_1_out_22),
    .out_26(rf_1_out_26), .out_30(rf_1_out_30), .out_7(rf_1_out_7), .out_11(rf_1_out_11),
    .out_15(rf_1_out_15), .out_19(rf_1_out_19), .out_23(rf_1_out_23), .out_27(rf_1_out_27),
    .out_31(rf_1_out_31), .out_8(rf_1_out_8), .out_12(rf_1_out_12), .out_16(rf_1_out_16),
    .out_20(rf_1_out_20), .out_24(rf_1_out_24), .out_28(rf_1_out_28), .out_32(rf_1_out_32),
    .out_9(rf_1_out_9), .out_13(rf_1_out_13), .out_17(rf_1_out_17), .out_21(rf_1_out_21),
    .out_25(rf_1_out_25), .out_29(rf_1_out_29), .out_33(rf_1_out_33), .in_4(multiplexer_1_out),
    .in_5(button_1_out), .in_3(rom_1_data));
  DotMatrix #(.inputtype("row"), .matrixcols(28), .matrixrows(28)) dotmatrix_1 (
    .row0(rf_1_out_6), .row1(rf_1_out_7), .row2(rf_1_out_8), .row3(rf_1_out_9), .row4(rf_1_out_10),
    .row5(rf_1_out_11), .row6(rf_1_out_12), .row7(rf_1_out_13), .row8(rf_1_out_14), .row9(rf_1_out_15),
    .row10(rf_1_out_16), .row11(rf_1_out_17), .row12(rf_1_out_18), .row13(rf_1_out_19), .row14(rf_1_out_20),
    .row15(rf_1_out_21), .row16(rf_1_out_22), .row17(rf_1_out_23), .row18(rf_1_out_24), .row19(rf_1_out_25),
    .row20(rf_1_out_26), .row21(rf_1_out_27), .row22(rf_1_out_28), .row23(rf_1_out_29), .row24(rf_1_out_30),
    .row25(rf_1_out_31), .row26(rf_1_out_32), .row27(rf_1_out_33));
  ROM #(.addrWidth(10), .dataWidth(16)) rom_3 (.addr(counter_3_q), .data(rom_3_data));  // open: sel
  ROM #(.addrWidth(10), .dataWidth(16)) rom_4 (.addr(counter_3_q), .data(rom_4_data));  // open: sel
  ROM #(.addrWidth(10), .dataWidth(16)) rom_5 (.addr(counter_3_q), .data(rom_5_data));  // open: sel
  ROM #(.addrWidth(10), .dataWidth(16)) rom_6 (.addr(counter_3_q), .data(rom_6_data));  // open: sel
  D_Flip_Flop d_ff_1 (.clk(counter_7_carry), .D(1'b1), .Q(d_ff_1_q), .reset(button_1_out));  // open: Qn, preset, en
  Multiplexer #(.select(3), .width(16), .enable("false")) multiplexer_6 (
    .in0(rom_3_data), .in1(rom_4_data), .in2(rom_2_data), .in3(rom_5_data), .in4(rom_6_data),
    .out(multiplexer_6_out), .sel(counter_4_q));  // open: in5, in6, in7
  Register #(.width(32)) register_1 (
    .D(multiplexer_9_out), .en(decoder_1_out0), .Q(register_1_q), .clk(multiplexer_3_out), .clr(button_1_out));
  assign bit_extender_2_out = {{31{1'b0}}, multiplexer_5_out};  // Bit_Extender bit_extender_2
  Multiplier #(.width(32)) multiplier_1 (
    .a(bit_extender_2_out), .b(bit_extender_3_out), .out(multiplier_1_out));  // open: cin, cout
  assign bit_extender_3_out = {{16{multiplexer_6_out[15]}}, multiplexer_6_out};  // Bit_Extender bit_extender_3
  Adder #(.width(32)) adder_1 (.a(multiplexer_8_out), .b(bit_extender_4_out), .out(adder_1_out));  // open: cin, cout
  Register #(.width(32)) register_2 (
    .D(multiplexer_9_out), .en(decoder_1_out1), .Q(register_2_q), .clk(multiplexer_3_out), .clr(button_1_out));
  Comparator #(.width(32)) comparator_1 (.a(adder_1_out), .b({32{1'b0}}), .lt(comparator_1_lt));  // open: gt, eq
  Register #(.width(32)) register_3 (
    .D(multiplexer_9_out), .en(decoder_1_out3), .Q(register_3_q), .clk(multiplexer_3_out), .clr(button_1_out));
  Register #(.width(32)) register_4 (
    .D(multiplexer_9_out), .en(decoder_1_out2), .Q(register_4_q), .clk(multiplexer_3_out), .clr(button_1_out));
  Multiplexer #(.width(32), .enable("false")) multiplexer_7 (
    .in0(adder_1_out), .in1({32{1'b0}}), .out(multiplexer_7_out), .sel(comparator_1_lt));
  Register #(.width(32)) register_5 (
    .D(multiplexer_9_out), .en(decoder_1_out4), .Q(register_5_q), .clk(multiplexer_3_out), .clr(button_1_out));
  Hex_Digit_Display hex_digit_display_3 (.value(multiplexer_17_out));  // open: dp
  Adder #(.width(32)) adder_2 (.a(multiplier_1_out), .b(multiplexer_8_out), .out(adder_2_out));  // open: cin, cout
  Multiplexer #(.select(3), .width(32), .enable("false")) multiplexer_8 (
    .in0(register_1_q), .in1(register_2_q), .in2(register_4_q), .in3(register_3_q), .in4(register_5_q),
    .out(multiplexer_8_out), .sel(multiplexer_4_out));  // open: in5, in6, in7
  D_Flip_Flop d_ff_2 (.clk(counter_5_carry), .D(1'b1), .Q(d_ff_2_q), .reset(button_1_out));  // open: Qn, preset, en
  LED led_1 (.in(d_ff_4_q));
  Multiplexer #(.width(32), .enable("false")) multiplexer_9 (
    .in0(adder_2_out), .in1(multiplexer_7_out), .out(multiplexer_9_out), .sel(d_ff_2_q));
  Counter #(.width(3), .max('h4)) counter_6 (
    .count(d_ff_2_q), .Q(counter_6_q), .carry(counter_6_carry), .clk(multiplexer_3_out), .clr(button_1_out));  // open: load, D
  Counter #(.width(1), .max('h1)) counter_7 (
    .count(counter_6_carry), .carry(counter_7_carry), .clk(multiplexer_3_out), .clr(button_1_out));  // open: load, D, Q
  Multiplexer #(.enable("false")) multiplexer_10 (
    .in0(1'b0), .in1(multiplexer_1_out), .out(multiplexer_10_out), .sel(d_ff_1_q));
  ROM #(.addrWidth(3), .dataWidth(16)) rom_7 (.addr(counter_6_q), .data(rom_7_data));  // open: sel
  Multiplexer #(.enable("false")) multiplexer_11 (
    .in0(multiplexer_10_out), .in1(1'b0), .out(multiplexer_11_out), .sel(d_ff_4_q));
  assign bit_extender_4_out = {{16{rom_7_data[15]}}, rom_7_data};  // Bit_Extender bit_extender_4
  Counter #(.width(3), .max('h4)) counter_8 (
    .Q(counter_8_q), .carry(counter_8_carry), .clk(multiplexer_11_out), .clr(button_1_out));  // open: load, D, count
  Counter #(.width(4), .max('hf)) counter_9 (
    .count(counter_8_carry), .Q(counter_9_q), .carry(counter_9_carry), .clk(multiplexer_11_out),
    .clr(button_1_out));  // open: load, D
  Multiplexer #(.select(3), .width(32), .enable("false")) multiplexer_12 (
    .in0(register_1_q), .in1(register_2_q), .in2(register_4_q), .in3(register_3_q), .in4(register_5_q),
    .out(multiplexer_12_out), .sel(counter_8_q));  // open: in5, in6, in7
  ROM #(.addrWidth(3), .dataWidth(16)) rom_8 (.addr(counter_8_q), .data(rom_8_data));  // open: sel
  ROM #(.addrWidth(3), .dataWidth(16)) rom_9 (.addr(counter_8_q), .data(rom_9_data));  // open: sel
  ROM #(.addrWidth(3), .dataWidth(16)) rom_10 (.addr(counter_8_q), .data(rom_10_data));  // open: sel
  ROM #(.addrWidth(3), .dataWidth(16)) rom_11 (.addr(counter_8_q), .data(rom_11_data));  // open: sel
  ROM #(.addrWidth(3), .dataWidth(16)) rom_12 (.addr(counter_8_q), .data(rom_12_data));  // open: sel
  ROM #(.addrWidth(3), .dataWidth(16)) rom_13 (.addr(counter_8_q), .data(rom_13_data));  // open: sel
  ROM #(.addrWidth(3), .dataWidth(16)) rom_14 (.addr(counter_8_q), .data(rom_14_data));  // open: sel
  ROM #(.addrWidth(3), .dataWidth(16)) rom_15 (.addr(counter_8_q), .data(rom_15_data));  // open: sel
  ROM #(.addrWidth(3), .dataWidth(16)) rom_16 (.addr(counter_8_q), .data(rom_16_data));  // open: sel
  ROM #(.addrWidth(3), .dataWidth(16)) rom_17 (.addr(counter_8_q), .data(rom_17_data));  // open: sel
  Multiplexer #(.select(4), .width(16), .enable("false")) multiplexer_13 (
    .in0(rom_8_data), .in1(rom_9_data), .in2(rom_10_data), .in3(rom_11_data), .in4(rom_12_data),
    .in5(rom_13_data), .in6(rom_14_data), .in7(rom_15_data), .in8(rom_16_data), .in9(rom_17_data),
    .out(multiplexer_13_out), .sel(multiplexer_14_out));  // open: in10, in11, in12, in13, in14, in15
  Multiplexer #(.width(4), .enable("false")) multiplexer_14 (
    .in0(counter_9_q), .in1(counter_10_q), .out(multiplexer_14_out), .sel(d_ff_3_q));
  assign bit_extender_5_out = {{16{multiplexer_13_out[15]}}, multiplexer_13_out};  // Bit_Extender bit_extender_5
  Decoder #(.select(4), .enable("false")) decoder_2 (
    .out0(decoder_2_out0), .out1(decoder_2_out1), .out2(decoder_2_out2), .out3(decoder_2_out3),
    .out4(decoder_2_out4), .out5(decoder_2_out5), .out6(decoder_2_out6), .out7(decoder_2_out7),
    .out8(decoder_2_out8), .out9(decoder_2_out9), .sel(multiplexer_14_out));  // open: out10, out11, out12, out13, out14, out15
  Multiplier #(.width(32)) multiplier_2 (
    .a(bit_extender_5_out), .b(multiplexer_12_out), .out(multiplier_2_out));  // open: cin, cout
  D_Flip_Flop d_ff_3 (.clk(counter_9_carry), .D(1'b1), .Q(d_ff_3_q), .reset(button_1_out));  // open: Qn, preset, en
  Adder #(.width(32)) adder_3 (.a(multiplexer_16_out), .b(multiplier_2_out), .out(adder_3_out));  // open: cin, cout
  Register #(.width(32)) register_6 (
    .D(multiplexer_15_out), .en(decoder_2_out0), .Q(register_6_q), .clk(multiplexer_11_out),
    .clr(button_1_out));
  Counter #(.width(4), .max('h9)) counter_10 (
    .count(d_ff_3_q), .Q(counter_10_q), .carry(counter_10_carry), .clk(multiplexer_11_out), .clr(button_1_out));  // open: load, D
  Multiplexer #(.width(32), .enable("false")) multiplexer_15 (
    .in0(adder_3_out), .in1(adder_4_out), .out(multiplexer_15_out), .sel(d_ff_3_q));
  Register #(.width(32)) register_7 (
    .D(multiplexer_15_out), .en(decoder_2_out2), .Q(register_7_q), .clk(multiplexer_11_out),
    .clr(button_1_out));
  Register #(.width(32)) register_8 (
    .D(multiplexer_15_out), .en(decoder_2_out1), .Q(register_8_q), .clk(multiplexer_11_out),
    .clr(button_1_out));
  Register #(.width(32)) register_9 (
    .D(multiplexer_15_out), .en(decoder_2_out3), .Q(register_9_q), .clk(multiplexer_11_out),
    .clr(button_1_out));
  ROM #(.addrWidth(4), .dataWidth(16)) rom_18 (.addr(counter_10_q), .data(rom_18_data));  // open: sel
  Register #(.width(32)) register_10 (
    .D(multiplexer_15_out), .en(decoder_2_out4), .Q(register_10_q), .clk(multiplexer_11_out),
    .clr(button_1_out));
  assign bit_extender_6_out = {{16{rom_18_data[15]}}, rom_18_data};  // Bit_Extender bit_extender_6
  Register #(.width(32)) register_11 (
    .D(multiplexer_15_out), .en(decoder_2_out6), .Q(register_11_q), .clk(multiplexer_11_out),
    .clr(button_1_out));
  Register #(.width(32)) register_12 (
    .D(multiplexer_15_out), .en(decoder_2_out5), .Q(register_12_q), .clk(multiplexer_11_out),
    .clr(button_1_out));
  D_Flip_Flop d_ff_4 (.clk(counter_10_carry), .D(1'b1), .Q(d_ff_4_q), .reset(button_1_out));  // open: Qn, preset, en
  Register #(.width(32)) register_13 (
    .D(multiplexer_15_out), .en(decoder_2_out7), .Q(register_13_q), .clk(multiplexer_11_out),
    .clr(button_1_out));
  Register #(.width(32)) register_14 (
    .D(multiplexer_15_out), .en(decoder_2_out8), .Q(register_14_q), .clk(multiplexer_11_out),
    .clr(button_1_out));
  Register #(.width(32)) register_15 (
    .D(multiplexer_15_out), .en(decoder_2_out9), .Q(register_15_q), .clk(multiplexer_11_out),
    .clr(button_1_out));
  Multiplexer #(.select(4), .width(32), .enable("false")) multiplexer_16 (
    .in0(register_6_q), .in1(register_8_q), .in2(register_7_q), .in3(register_9_q), .in4(register_10_q),
    .in5(register_12_q), .in6(register_11_q), .in7(register_13_q), .in8(register_14_q), .in9(register_15_q),
    .out(multiplexer_16_out), .sel(multiplexer_14_out));  // open: in10, in11, in12, in13, in14, in15
  Adder #(.width(32)) adder_4 (.a(bit_extender_6_out), .b(multiplexer_16_out), .out(adder_4_out));  // open: cin, cout
  max10 max10_1 (
    .in_1(register_6_q), .in_2(register_8_q), .in_3(register_7_q), .in_4(register_9_q), .in_5(register_10_q),
    .in_6(register_12_q), .in_7(register_11_q), .in_8(register_13_q), .in_9(register_14_q),
    .in_10(register_15_q), .out_11(max10_1_out_11));
  Multiplexer #(.width(4), .enable("false")) multiplexer_17 (
    .in0(4'b0000), .in1(max10_1_out_11), .out(multiplexer_17_out), .sel(d_ff_4_q));

  // Notes on the sheet:
  //   contents of rom_1 (hex, n*v repeats v):
  //   4*0 30 70 e0 e0 40c0 c180 c180 1c380 18700 38600 78e00 ffc00 1cfe00 307e00 6000 e000 c000 1c000
  //   38000 10000
  //   contents of rom_2 (hex, n*v repeats v):
  //   4 fffc fffa 8 8 ffff 6 fff8 fffd fffe 8 1 4 3 1 fff9 6 3 3 fff9 9 fff8 fff8 9 fffd 7 fffd fff8 fffb
  //   fffc fffe fffc 2 fffe fffe 1 7 fff4 0 fffe 6 fffd fff2 fff1 4 fff7 4 fff5 ffef fffb fffe fff8 fff9 0
  //   fffc fff9 fff9 ffff 8 fffa 4 fff7 0 fff7 fff4 ffeb ffec fff1 fff1 ffe4 ffeb ffea ffdf ffea ffe2 ffd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
  //   contents of rom_3 (hex, n*v repeats v):
  //   fffb 6 8 3 3 4 fffa fffd 0 2 2 5 4 5 fffa 2 fffb 0 2 fffd 7 fff9 fffb 1 6 fffb 0 5 2 fffb fffd 2 4
  //   fff9 2 fffa 7 d fffe d 1 1 2 fffd ffee fffc fffd 4 2 fff8 6 fffe fff9 5 3 3 4 fffb 6 3 0 2 fffc fffd
  //   fffe fff4 fffa ffff ffff ffff fff1 fff9 fffa 1 a 1 12 8 fffd 4 3 fff7 fffb 4 5 2 fffe fffe 4 fffd 9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
  //   contents of rom_4 (hex, n*v repeats v):
  //   5 6 1 fffe 6 fffd fff9 fffe 5 0 6 fffa fff9 0 0 6 8 fffb fffe fff9 fff8 2 2 3 fff8 fffa fffd 8 fffc
  //   fffb fffa 0 fff8 fffa c e 15 9 9 8 10 17 10 17 20 d 5 8 15 1 8 6 1 0 fffa ffff 2 6 0 0 6 2 17 1f 1f
  //   20 25 2e 2d 2e 32 2d 31 25 28 1a 1d 18 f 14 18 e 9 ffff fffa 4 4 fff8 fffe fff5 17 19 1b 1f 18 26 15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
  //   contents of rom_5 (hex, n*v repeats v):
  //   fffd 8 fffc 1 fffe 3 fffd 9 0 7 fffd fffd 3 6 fffc 1 5 fffe 0 fffd 7 ffff fffa ffff fff8 2 1 fffd 4
  //   5 fffd fffa ffff 1 fff9 6 1 7 c 16 9 12 fff7 fffb ffee fffc d 7 11 1 9 5 fffc fffc fff8 fffd fffe 7
  //   2 fffb 6 fffa 12 a 12 19 26 1d 23 15 19 14 18 10 1d 27 21 21 13 7 4 fff7 fff8 fff9 fff9 fff9 9 fffd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
  //   contents of rom_6 (hex, n*v repeats v):
  //   3 8 fffc fffb 5 1 6 3 5 fff7 2 4 2 1 fff9 fffb fff8 1 7 8 4 3 5 0 3 ffff 6 fff8 3 0 fff9 ffff fffd
  //   fffe fffb c 1 fff2 ffef fff7 1 3 fff7 fff7 fff5 fffe fffe 6 ffff fff3 fff8 fffd fff8 fff8 9 6 2 6 3
  //   fffb fffe 5 fffd fff9 fff8 ffdf ffe4 ffe9 ffdc ffe2 ffe6 fff0 fff2 fff7 fff4 ffff fff6 2 fff6 fff7
  //   ff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
  //   contents of rom_7 (hex, n*v repeats v):
  //   1 fffe a 32 fff1
  //   contents of rom_8 (hex, n*v repeats v):
  //   ff84 fffa 10 11 50
  //   contents of rom_9 (hex, n*v repeats v):
  //   5e 4b ffb2 ff86 fff9
  //   contents of rom_10 (hex, n*v repeats v):
  //   ffb5 5e 9 ffe2 fff8
  //   contents of rom_11 (hex, n*v repeats v):
  //   19 fffd 4e ffaf fff4
  //   contents of rom_12 (hex, n*v repeats v):
  //   27 ffbb ff80 24 5f
  //   contents of rom_13 (hex, n*v repeats v):
  //   16 fffa 2a c ffe9
  //   contents of rom_14 (hex, n*v repeats v):
  //   ffef 4b ffad 26 ffef
  //   contents of rom_15 (hex, n*v repeats v):
  //   ffe4 ffdc 2e 3f ff65
  //   contents of rom_16 (hex, n*v repeats v):
  //   3a 1f ffe2 ffeb 36
  //   contents of rom_17 (hex, n*v repeats v):
  //   46 ffc4 ffd3 38 ffbc
  //   contents of rom_18 (hex, n*v repeats v):
  //   ffc7 23 22 11 30 ffd5 ffd0 40 ffb9 24
endmodule

module max10 (
  input  [31:0] in_1,
  input  [31:0] in_2,
  input  [31:0] in_3,
  input  [31:0] in_4,
  input  [31:0] in_5,
  input  [31:0] in_6,
  input  [31:0] in_7,
  input  [31:0] in_8,
  input  [31:0] in_9,
  input  [31:0] in_10,
  output [3:0] out_11
);

  wire comparator_1_gt, comparator_1_lt, comparator_2_gt, comparator_2_lt, comparator_3_gt, comparator_3_lt,
       comparator_4_gt, comparator_4_lt, comparator_5_gt, comparator_5_lt, comparator_6_lt, comparator_7_lt,
       comparator_8_lt, comparator_9_lt;
  wire [3:0] multiplexer_6_out, multiplexer_7_out, multiplexer_8_out, multiplexer_9_out, multiplexer_10_out,
       multiplexer_11_out, multiplexer_13_out, multiplexer_16_out;
  wire [31:0] multiplexer_1_out, multiplexer_2_out, multiplexer_3_out, multiplexer_4_out, multiplexer_5_out,
       multiplexer_12_out, multiplexer_14_out, multiplexer_15_out;

  Comparator #(.width(32)) comparator_1 (.a(in_1), .b(in_2), .gt(comparator_1_gt), .lt(comparator_1_lt));  // open: eq
  Comparator #(.width(32)) comparator_2 (.a(in_3), .b(in_4), .gt(comparator_2_gt), .lt(comparator_2_lt));  // open: eq
  Comparator #(.width(32)) comparator_3 (.a(in_5), .b(in_6), .gt(comparator_3_gt), .lt(comparator_3_lt));  // open: eq
  Comparator #(.width(32)) comparator_4 (.a(in_7), .b(in_8), .gt(comparator_4_gt), .lt(comparator_4_lt));  // open: eq
  Comparator #(.width(32)) comparator_5 (.a(in_9), .b(in_10), .gt(comparator_5_gt), .lt(comparator_5_lt));  // open: eq
  Multiplexer #(.width(32), .enable("false")) multiplexer_1 (
    .in0(in_1), .in1(in_2), .out(multiplexer_1_out), .sel(comparator_1_lt));
  Multiplexer #(.width(32), .enable("false")) multiplexer_2 (
    .in0(in_3), .in1(in_4), .out(multiplexer_2_out), .sel(comparator_2_lt));
  Multiplexer #(.width(32), .enable("false")) multiplexer_3 (
    .in0(in_5), .in1(in_6), .out(multiplexer_3_out), .sel(comparator_3_lt));
  Multiplexer #(.width(32), .enable("false")) multiplexer_4 (
    .in0(in_7), .in1(in_8), .out(multiplexer_4_out), .sel(comparator_4_lt));
  Multiplexer #(.width(32), .enable("false")) multiplexer_5 (
    .in0(in_9), .in1(in_10), .out(multiplexer_5_out), .sel(comparator_5_lt));
  Multiplexer #(.width(4), .enable("false")) multiplexer_6 (
    .in0(4'b0001), .in1(4'b0000), .out(multiplexer_6_out), .sel(comparator_1_gt));
  Multiplexer #(.width(4), .enable("false")) multiplexer_7 (
    .in0(4'b0011), .in1(4'b0010), .out(multiplexer_7_out), .sel(comparator_2_gt));
  Multiplexer #(.width(4), .enable("false")) multiplexer_8 (
    .in0(4'b0101), .in1(4'b0100), .out(multiplexer_8_out), .sel(comparator_3_gt));
  Multiplexer #(.width(4), .enable("false")) multiplexer_9 (
    .in0(4'b0111), .in1(4'b0110), .out(multiplexer_9_out), .sel(comparator_4_gt));
  Multiplexer #(.width(4), .enable("false")) multiplexer_10 (
    .in0(4'b1001), .in1(4'b1000), .out(multiplexer_10_out), .sel(comparator_5_gt));
  Comparator #(.width(32)) comparator_6 (
    .a(multiplexer_1_out), .b(multiplexer_2_out), .lt(comparator_6_lt));  // open: gt, eq
  Comparator #(.width(32)) comparator_7 (
    .a(multiplexer_4_out), .b(multiplexer_5_out), .lt(comparator_7_lt));  // open: gt, eq
  Multiplexer #(.width(4), .enable("false")) multiplexer_11 (
    .in0(multiplexer_6_out), .in1(multiplexer_7_out), .out(multiplexer_11_out), .sel(comparator_6_lt));
  Multiplexer #(.width(32), .enable("false")) multiplexer_12 (
    .in0(multiplexer_1_out), .in1(multiplexer_2_out), .out(multiplexer_12_out), .sel(comparator_6_lt));
  Multiplexer #(.width(4), .enable("false")) multiplexer_13 (
    .in0(multiplexer_9_out), .in1(multiplexer_10_out), .out(multiplexer_13_out), .sel(comparator_7_lt));
  Multiplexer #(.width(32), .enable("false")) multiplexer_14 (
    .in0(multiplexer_4_out), .in1(multiplexer_5_out), .out(multiplexer_14_out), .sel(comparator_7_lt));
  Comparator #(.width(32)) comparator_8 (
    .a(multiplexer_12_out), .b(multiplexer_3_out), .lt(comparator_8_lt));  // open: gt, eq
  Multiplexer #(.width(32), .enable("false")) multiplexer_15 (
    .in0(multiplexer_12_out), .in1(multiplexer_3_out), .out(multiplexer_15_out), .sel(comparator_8_lt));
  Multiplexer #(.width(4), .enable("false")) multiplexer_16 (
    .in0(multiplexer_11_out), .in1(multiplexer_8_out), .out(multiplexer_16_out), .sel(comparator_8_lt));
  Comparator #(.width(32)) comparator_9 (
    .a(multiplexer_15_out), .b(multiplexer_14_out), .lt(comparator_9_lt));  // open: gt, eq
  Multiplexer #(.width(4), .enable("false")) multiplexer_17 (
    .in0(multiplexer_16_out), .in1(multiplexer_13_out), .out(out_11), .sel(comparator_9_lt));
endmodule

module relu (
  input  [31:0] in_1,
  output [31:0] out_2
);

  wire comparator_1_lt;

  Comparator #(.width(32)) comparator_1 (.a(in_1), .b({32{1'b0}}), .lt(comparator_1_lt));  // open: gt, eq
  Multiplexer #(.width(32), .enable("false")) multiplexer_1 (
    .in0(in_1), .in1({32{1'b0}}), .out(out_2), .sel(comparator_1_lt));
endmodule
